// Logisim project BeLe251C.circ as structural Verilog: 1 circuit, main circuit main
module main (
  output [31:0] BigEndian,
  output [31:0] LittleEndian
);


  assign BigEndian = 32'h65028051;
  assign LittleEndian = 32'h51800265;

  // Notes on the sheet:
  //   0x12345678
  //   0x12345679
  //   0x1234567A
  //   0x1234567B
endmodule
