// Logisim project ByteAlignment.circ as structural Verilog
module MEM16 (
  input  [6:0] in_1,
  input  [1:0] Inst,
  output [15:0] CPU
);

  wire and_1_out;
  wire [7:0] multiplexer_1_out;
  wire [15:0] LH, LHU, LW;

  ROM #(.addrWidth(6), .dataWidth(16)) rom_1 (.addr(in_1[6:1]), .data(LW));
  and and_1 (and_1_out, in_1[0], ~Inst[0], ~Inst[1]);  // AND_Gate
  LED NoAlineado (.in(and_1_out));
  Multiplexer #(.width(8)) multiplexer_1 (.in0(LW[7:0]), .in1(LW[15:8]), .out(multiplexer_1_out), .sel(in_1[0]));
  Multiplexer #(.select(2), .width(16)) multiplexer_2 (
    .in0(LW), .in1(LH), .in2(LHU), .out(CPU), .sel(Inst));  // open: in3
  assign LH = {{8{multiplexer_1_out[7]}}, multiplexer_1_out};  // Bit_Extender bit_extender_1
  assign LHU = {{8{1'b0}}, multiplexer_1_out};  // Bit_Extender bit_extender_2

  // Other names for the same wires on the sheet: bms = in_1[0]

  // Notes on the sheet:
  //   LW xx - 00
  //   LH xx - 01
  //   LHU xx - 10
  //   contents of rom_1 (hex, n*v repeats v):
  //   2312 2321 3333 2111 21cc ccaa ddee fede 323d
endmodule

module MEM32 (
  input  [7:0] in_1,
  input  [2:0] Instr,
  output [31:0] Dato,
  output [5:0] out_4
);

  wire and_1_out, and_2_out, LW, or_1_out;
  wire [7:0] multiplexer_2_out, rom_1_data, rom_1_data_2, rom_1_data_3, rom_1_data_4;
  wire [15:0] multiplexer_1_out;
  wire [31:0] bit_extender_1_out, bit_extender_2_out, bit_extender_3_out, bit_extender_4_out;

  and and_1 (and_1_out, Instr[0], in_1[1], in_1[0]);
  or or_1 (or_1_out, in_1[0], in_1[1]);
  ROM #(.addrWidth(6), .dataWidth(32)) rom_1 (
    .addr(in_1[7:2]), .data({rom_1_data_4, rom_1_data_3, rom_1_data_2, rom_1_data}));
  nor nor_1 (LW, Instr[0], Instr[1], Instr[2]);
  LED Unaligned16 (.in(and_1_out));
  and and_2 (and_2_out, or_1_out, LW);
  LED Unaligned32 (.in(and_2_out));
  Multiplexer #(.select(2), .width(16)) multiplexer_1 (
    .in0({rom_1_data_2, rom_1_data}), .in1({rom_1_data_3, rom_1_data_2}), .in2({rom_1_data_4, rom_1_data_3}),
    .in3({rom_1_data_4, rom_1_data_3}), .out(multiplexer_1_out), .sel(in_1[1:0]));
  assign bit_extender_1_out = {{16{multiplexer_1_out[15]}}, multiplexer_1_out};  // Bit_Extender bit_extender_1
  assign bit_extender_2_out = {{16{1'b0}}, multiplexer_1_out};  // Bit_Extender bit_extender_2
  Multiplexer #(.select(2), .width(8)) multiplexer_2 (
    .in0(rom_1_data), .in1(rom_1_data_2), .in2(rom_1_data_3), .in3(rom_1_data_4), .out(multiplexer_2_out),
    .sel(in_1[1:0]));
  Multiplexer #(.select(3), .width(32)) multiplexer_3 (
    .in0({rom_1_data_4, rom_1_data_3, rom_1_data_2, rom_1_data}), .in1(bit_extender_1_out),
    .in2(bit_extender_3_out), .in3(bit_extender_2_out), .in4(bit_extender_4_out), .out(Dato), .sel(Instr));  // open: in5, in6, in7
  assign bit_extender_3_out = {{24{multiplexer_2_out[7]}}, multiplexer_2_out};  // Bit_Extender bit_extender_3
  assign bit_extender_4_out = {{24{1'b0}}, multiplexer_2_out};  // Bit_Extender bit_extender_4

  assign out_4 = in_1[7:2];

  // Other names for the same wires on the sheet: bms2[1:0] = in_1[1:0]; Inst[2:0] = Instr; LH = Instr[0]

  // Notes on the sheet:
  //   LHU 011
  //   LBU 100
  //   LW 000
  //   LH 001
  //   LB 010
  //   contents of rom_1 (hex, n*v repeats v):
  //   12345678 9abcdef0 12342341 343bbdcc
endmodule
