// Logisim project ModelosUnidad0AC251C.circ as structural Verilog
module CPUMicroprogramada251C (
);

  wire ALUOP, button_1_out, button_2_out, button_3_out, button_4_out, button_5_out, clock_1_out, clock_2_out,
       clock_3_out, clock_4_out, clock_5_out, clock_6_out, digital_oscilloscope_1_p10, MBROE, nor_1_out,
       nor_2_out, R0OE, R0WE, R1OE, R1WE, RTROE, RTRWE;
  wire [3:0] A, adder_1_out, B, MBR_q, multiplexer_1_out, R0_q, R1_q, RTR_q, subtractor_1_out;
  wire [4:0] counter_1_q;

  Counter #(.max('h1f), .width(5)) counter_1 (
    .Q(counter_1_q), .clk(clock_1_out), .clr(button_1_out));  // open: load, D, count, carry, up
  Button button_1 (.out(button_1_out));
  Clock clock_1 (.out(clock_1_out));
  ROM #(.addrWidth(5)) rom_1 (.addr(counter_1_q), .data({RTROE, RTRWE, ALUOP, R0OE, R0WE, R1OE, R1WE, MBROE}));
  assign B = nor_1_out ? 4'b0001 : 4'bz;  // Controlled_Buffer controlled_buffer_1
  nor nor_1 (nor_1_out, R0OE, R1OE);
  Register #(.width(4)) R0 (.D(A), .en(R0WE), .clk(clock_2_out), .Q(R0_q), .clr(button_2_out));
  Clock clock_2 (.out(clock_2_out));
  Button button_2 (.out(button_2_out));
  assign A = nor_2_out ? 4'b0000 : 4'bz;  // Controlled_Buffer controlled_buffer_2
  nor nor_2 (nor_2_out, RTROE, MBROE);
  assign B = R0OE ? R0_q : 4'bz;  // Controlled_Buffer controlled_buffer_3
  Hex_Digit_Display u_A (.value(A));  // open: dp
  Register #(.width(4)) R1 (.D(A), .en(R1WE), .clk(clock_3_out), .Q(R1_q), .clr(button_3_out));
  Clock clock_3 (.out(clock_3_out));
  LED led_1 (.in(RTROE));
  Hex_Digit_Display u_B (.value(B));  // open: dp
  Adder #(.width(4)) adder_1 (.a(A), .b(B), .out(adder_1_out));  // open: cin, cout
  Subtractor #(.width(4)) subtractor_1 (.a(A), .b(B), .out(subtractor_1_out));  // open: bin, bout
  Button button_3 (.out(button_3_out));
  LED led_2 (.in(RTRWE));
  Hex_Digit_Display Res (.value(multiplexer_1_out));  // open: dp
  Multiplexer #(.width(4)) multiplexer_1 (
    .in0(adder_1_out), .in1(subtractor_1_out), .out(multiplexer_1_out), .sel(ALUOP));
  assign B = R1OE ? R1_q : 4'bz;  // Controlled_Buffer controlled_buffer_4
  LED led_3 (.in(ALUOP));
  Register #(.width(4)) RTR (.D(multiplexer_1_out), .en(RTRWE), .clk(clock_4_out), .Q(RTR_q), .clr(button_4_out));
  Clock clock_4 (.out(clock_4_out));
  Clock clock_5 (.out(clock_5_out));
  LED led_4 (.in(R0OE));
  Button button_4 (.out(button_4_out));
  Register #(.width(4)) MBR (.en(1'b0), .clk(clock_5_out), .Q(MBR_q), .clr(button_5_out));  // open: D
  Button button_5 (.out(button_5_out));
  LED led_5 (.in(R0WE));
  assign A = RTROE ? RTR_q : 4'bz;  // Controlled_Buffer controlled_buffer_5
  assign A = MBROE ? MBR_q : 4'bz;  // Controlled_Buffer controlled_buffer_6
  LED led_6 (.in(R1OE));
  Clock clock_6 (.out(clock_6_out));
  LED led_7 (.in(R1WE));
  // Digital_Oscilloscope digital_oscilloscope_1: pin names not known; wires that end beside it: clock_6_out, RTROE, RTRWE, ALUOP, R0OE, R0WE, R1OE, R1WE, MBROE, digital_oscilloscope_1_p10
  Button button_6 (.out(digital_oscilloscope_1_p10));
  LED led_8 (.in(MBROE));

  // Notes on the sheet:
  //   contents of rom_1 (hex, n*v repeats v):
  //   9 51 c4 88
endmodule

module CPUCableada251C (
);

  wire button_1_out, button_2_out, button_3_out, button_4_out, clock_1_out, clock_2_out, clock_3_out,
       clock_4_out, clock_5_out, demultiplexer_1_out0, demultiplexer_1_out1, demultiplexer_1_out2,
       demultiplexer_1_out3, Inm, Signo;
  wire [1:0] RD, RS1, RS2;
  wire [3:0] bit_extender_1_out;
  wire [4:0] adder_1_out, BusDatos, multiplexer_1_out, multiplexer_2_out, multiplexer_3_out, R0_q, R1_q,
       R2_q, R3_q, subtractor_1_out;
  wire [5:0] counter_1_q;

  Clock clock_1 (.out(clock_1_out));
  Demultiplexer #(.select(2)) demultiplexer_1 (
    .out0(demultiplexer_1_out0), .out1(demultiplexer_1_out1), .out2(demultiplexer_1_out2),
    .out3(demultiplexer_1_out3), .in(1'b1), .sel(RD));
  ROM #(.addrWidth(6)) rom_1 (.addr(counter_1_q), .data({Inm, Signo, RD, RS1, RS2}));
  Counter #(.max('h3f), .width(6)) counter_1 (
    .Q(counter_1_q), .clk(clock_1_out), .clr(button_1_out));  // open: load, D, count, carry, up
  Button button_1 (.out(button_1_out));
  Register #(.width(5)) R0 (.D(BusDatos), .en(demultiplexer_1_out0), .clk(clock_2_out), .Q(R0_q), .clr(1'b1));
  Clock clock_2 (.out(clock_2_out));
  Register #(.width(5)) R1 (.D(BusDatos), .en(demultiplexer_1_out1), .clk(clock_3_out), .Q(R1_q), .clr(button_2_out));
  Clock clock_3 (.out(clock_3_out));
  Button button_2 (.out(button_2_out));
  Register #(.width(5)) R2 (.D(BusDatos), .en(demultiplexer_1_out2), .clk(clock_4_out), .Q(R2_q), .clr(button_3_out));
  Clock clock_4 (.out(clock_4_out));
  Button button_3 (.out(button_3_out));
  Register #(.width(5)) R3 (.D(BusDatos), .en(demultiplexer_1_out3), .clk(clock_5_out), .Q(R3_q), .clr(button_4_out));
  Clock clock_5 (.out(clock_5_out));
  Button button_4 (.out(button_4_out));
  LED led_1 (.in(Inm));
  LED led_2 (.in(Signo));
  Multiplexer #(.select(2), .width(5)) multiplexer_1 (
    .in0(R0_q), .in1(R1_q), .in2(R2_q), .in3(R3_q), .out(multiplexer_1_out), .sel(RS1));
  Multiplexer #(.select(2), .width(5)) multiplexer_2 (
    .in0(R0_q), .in1(R1_q), .in2(R2_q), .in3(R3_q), .out(multiplexer_2_out), .sel(RS2));
  LED led_3 (.in(RD[1]));
  LED led_4 (.in(RD[0]));
  LED led_5 (.in(RS1[1]));
  LED led_6 (.in(RS1[0]));
  Adder #(.width(5)) adder_1 (.a(multiplexer_1_out), .b(multiplexer_2_out), .out(adder_1_out));  // open: cin, cout
  Subtractor #(.width(5)) subtractor_1 (
    .a(multiplexer_1_out), .b(multiplexer_2_out), .out(subtractor_1_out));  // open: bin, bout
  LED led_7 (.in(RS2[1]));
  LED led_8 (.in(RS2[0]));
  Multiplexer #(.width(5)) multiplexer_3 (
    .in0(adder_1_out), .in1(subtractor_1_out), .out(multiplexer_3_out), .sel(Signo));
  Multiplexer #(.width(5)) multiplexer_4 (.in0(multiplexer_3_out), .in1({Signo, RS1, RS2}), .out(BusDatos), .sel(Inm));
  Hex_Digit_Display hex_digit_display_1 (.value(bit_extender_1_out));  // open: dp
  Hex_Digit_Display hex_digit_display_2 (.value(BusDatos[3:0]));  // open: dp
  assign bit_extender_1_out = {{3{1'b0}}, BusDatos[4]};  // Bit_Extender bit_extender_1
endmodule
