// Logisim project RepasoFSE.circ as structural Verilog
module FullAdder (
  input  Cin,
  input  A,
  input  B,
  output S,
  output Cout
);

  wire and_1_out, and_2_out, and_3_out, xor_1_out;

  xor xor_1 (xor_1_out, A, B);
  and and_1 (and_1_out, A, B);
  and and_2 (and_2_out, A, Cin);
  and and_3 (and_3_out, Cin, B);
  xor xor_2 (S, xor_1_out, Cin);
  or or_1 (Cout, and_1_out, and_2_out, and_3_out);
endmodule

module FullSubstractor (
  input  A,
  input  B,
  input  Bin,
  output R,
  output Bo
);

  wire and_1_out, and_2_out, and_3_out, xor_1_out;

  xor xor_1 (xor_1_out, B, Bin);
  and and_1 (and_1_out, ~A, Bin);  // AND_Gate
  and and_2 (and_2_out, B, Bin);
  and and_3 (and_3_out, ~A, B);  // AND_Gate
  xor xor_2 (R, A, xor_1_out);
  or or_1 (Bo, and_1_out, and_2_out, and_3_out);
endmodule
