// Logisim project Parcial2u4.circ as structural Verilog: 11 circuits, main circuit main
module main (
  output [2:0] out_1
);

  wire clock_1_out;

  Clock clock_1 (.out(clock_1_out));
  T_Flip_Flop #(.trigger("falling")) t_ff_1 (.T(1'b1), .clk(clock_1_out), .Q(out_1[0]));  // open: Qn, reset, preset
  T_Flip_Flop #(.trigger("falling")) t_ff_2 (.T(1'b1), .clk(out_1[0]), .Q(out_1[1]));  // open: Qn, reset, preset
  T_Flip_Flop #(.trigger("falling")) t_ff_3 (.T(1'b1), .clk(out_1[1]), .Q(out_1[2]));  // open: Qn, reset, preset
endmodule

module RegLatch8Bits (
  input  [7:0] Din,
  input  Clk,
  input  R,
  output [7:0] Dout
);

  D_Flip_Flop d_ff_1 (.D(Din[7]), .clk(Clk), .Q(Dout[7]), .reset(R));  // open: Qn, preset
  D_Flip_Flop d_ff_2 (.D(Din[6]), .clk(Clk), .Q(Dout[6]), .reset(R));  // open: Qn, preset
  D_Flip_Flop d_ff_3 (.D(Din[5]), .clk(Clk), .Q(Dout[5]), .reset(R));  // open: Qn, preset
  D_Flip_Flop d_ff_4 (.D(Din[4]), .clk(Clk), .Q(Dout[4]), .reset(R));  // open: Qn, preset
  D_Flip_Flop d_ff_5 (.D(Din[3]), .clk(Clk), .Q(Dout[3]), .reset(R));  // open: Qn, preset
  D_Flip_Flop d_ff_6 (.D(Din[2]), .clk(Clk), .Q(Dout[2]), .reset(R));  // open: Qn, preset
  D_Flip_Flop d_ff_7 (.D(Din[1]), .clk(Clk), .Q(Dout[1]));  // open: Qn, preset, reset
  D_Flip_Flop d_ff_8 (.D(Din[0]), .clk(Clk), .Q(Dout[0]), .reset(R));  // open: Qn, preset
endmodule

module RegShift8Bits (
  input  Din,
  input  Clk,
  output [7:0] Dout
);

  D_Flip_Flop d_ff_1 (.D(Din), .clk(Clk), .Q(Dout[7]));  // open: Qn, preset, reset
  D_Flip_Flop d_ff_2 (.D(Dout[7]), .clk(Clk), .Q(Dout[6]));  // open: Qn, preset, reset
  D_Flip_Flop d_ff_3 (.D(Dout[6]), .clk(Clk), .Q(Dout[5]));  // open: Qn, preset, reset
  D_Flip_Flop d_ff_4 (.D(Dout[5]), .clk(Clk), .Q(Dout[4]));  // open: Qn, preset, reset
  D_Flip_Flop d_ff_5 (.D(Dout[4]), .clk(Clk), .Q(Dout[3]));  // open: Qn, preset, reset
  D_Flip_Flop d_ff_6 (.D(Dout[3]), .clk(Clk), .Q(Dout[2]));  // open: Qn, preset, reset
  D_Flip_Flop d_ff_7 (.D(Dout[2]), .clk(Clk), .Q(Dout[1]));  // open: Qn, preset, reset
  D_Flip_Flop d_ff_8 (.D(Dout[1]), .clk(Clk), .Q(Dout[0]));  // open: Qn, preset, reset
endmodule

module ParaleloASerie (
  input  [7:0] Din,
  input  Latch,
  input  R,
  input  Clk,
  output Dout
);

  wire d_ff_1_q, d_ff_2_q, d_ff_3_q, d_ff_4_q, d_ff_5_q, d_ff_6_q, d_ff_7_q, d_ff_8_q;
  wire [2:0] contadorascsincmodulo8_1_c;

  D_Flip_Flop d_ff_1 (.D(Din[7]), .clk(Latch), .Q(d_ff_1_q), .reset(R));  // open: Qn, preset
  D_Flip_Flop d_ff_2 (.D(Din[6]), .clk(Latch), .Q(d_ff_2_q), .reset(R));  // open: Qn, preset
  D_Flip_Flop d_ff_3 (.D(Din[5]), .clk(Latch), .Q(d_ff_3_q), .reset(R));  // open: Qn, preset
  D_Flip_Flop d_ff_4 (.D(Din[4]), .clk(Latch), .Q(d_ff_4_q), .reset(R));  // open: Qn, preset
  D_Flip_Flop d_ff_5 (.D(Din[3]), .clk(Latch), .Q(d_ff_5_q), .reset(R));  // open: Qn, preset
  Multiplexer #(.select(3)) multiplexer_1 (
    .in0(d_ff_8_q), .in1(d_ff_7_q), .in2(d_ff_6_q), .in3(d_ff_5_q), .in4(d_ff_4_q), .in5(d_ff_3_q),
    .in6(d_ff_2_q), .in7(d_ff_1_q), .out(Dout), .sel(contadorascsincmodulo8_1_c));
  ContadorAscSincModulo8 contadorascsincmodulo8_1 (.Clk(Clk), .C(contadorascsincmodulo8_1_c));
  D_Flip_Flop d_ff_6 (.D(Din[2]), .clk(Latch), .Q(d_ff_6_q), .reset(R));  // open: Qn, preset
  D_Flip_Flop d_ff_7 (.D(Din[1]), .clk(Latch), .Q(d_ff_7_q), .reset(R));  // open: Qn, preset
  D_Flip_Flop d_ff_8 (.D(Din[0]), .clk(Latch), .Q(d_ff_8_q), .reset(R));  // open: Qn, preset
endmodule

module ContadorAscAsincModulo8 (
  input  Clk,
  output [2:0] C
);

  T_Flip_Flop #(.trigger("falling")) t_ff_1 (.T(1'b1), .clk(Clk), .Q(C[0]));  // open: Qn, reset, preset
  T_Flip_Flop #(.trigger("falling")) t_ff_2 (.T(1'b1), .clk(C[0]), .Q(C[1]));  // open: Qn, reset, preset
  T_Flip_Flop #(.trigger("falling")) t_ff_3 (.T(1'b1), .clk(C[1]), .Q(C[2]));  // open: Qn, reset, preset
endmodule

module ContadorAscSincModulo8 (
  input  Clk,
  output [2:0] C
);

  wire and_1_out;

  T_Flip_Flop t_ff_1 (.T(1'b1), .clk(Clk), .Q(C[0]));  // open: Qn, reset, preset
  T_Flip_Flop t_ff_2 (.T(C[0]), .clk(Clk), .Q(C[1]));  // open: Qn, reset, preset
  and and_1 (and_1_out, C[0], C[1]);
  T_Flip_Flop t_ff_3 (.T(and_1_out), .clk(Clk), .Q(C[2]));  // open: Qn, reset, preset
endmodule

module E08 (
  input  [7:0] in_1,
  input  in_2,
  input  in_3,
  output [7:0] out_4
);

  wire clock_1_out, paraleloaserie_1_dout;

  Clock clock_1 (.out(clock_1_out));
  ParaleloASerie paraleloaserie_1 (.Din(in_1), .Latch(in_2), .R(in_3), .Clk(clock_1_out), .Dout(paraleloaserie_1_dout));
  RegShift8Bits regshift8bits_1 (.Din(paraleloaserie_1_dout), .Clk(clock_1_out), .Dout(out_4));
endmodule

module ContadorDescAsincModulo16 (
  input  Clk,
  input  in_2,
  output [3:0] C
);

  T_Flip_Flop t_ff_1 (.T(1'b1), .clk(Clk), .Q(C[0]));  // open: Qn, reset, preset
  T_Flip_Flop t_ff_2 (.T(1'b1), .clk(C[0]), .Q(C[1]));  // open: Qn, reset, preset
  T_Flip_Flop t_ff_3 (.T(1'b1), .clk(C[1]), .Q(C[2]));  // open: Qn, reset, preset
  T_Flip_Flop t_ff_4 (.T(1'b1), .clk(C[2]), .Q(C[3]));  // open: Qn, reset, preset
  // Digital_Oscilloscope digital_oscilloscope_1: pin names not known; wires that end beside it: Clk, C[3], C[2], C[1], C[0], in_2
endmodule

module ContadoAscSincModulo16 (
  input  Clk,
  output [3:0] C
);

  wire and_1_out, and_2_out;

  T_Flip_Flop t_ff_1 (.T(1'b1), .clk(Clk), .Q(C[0]));  // open: Qn, reset, preset
  T_Flip_Flop t_ff_2 (.T(C[0]), .clk(Clk), .Q(C[1]));  // open: Qn, reset, preset
  and and_1 (and_1_out, C[0], C[1]);
  T_Flip_Flop t_ff_3 (.T(and_1_out), .clk(Clk), .Q(C[2]));  // open: Qn, reset, preset
  and and_2 (and_2_out, and_1_out, C[2]);
  T_Flip_Flop t_ff_4 (.T(and_2_out), .clk(Clk), .Q(C[3]));  // open: Qn, reset, preset
endmodule

module OneHotJohnson5Bits (
  input  Clk,
  input  Tipo,
  output [4:0] Dout
);

  wire d_ff_5_qn, multiplexer_1_out, por_1_out;

  POR por_1 (.out(por_1_out));
  D_Flip_Flop d_ff_1 (.D(multiplexer_1_out), .clk(Clk), .Q(Dout[0]), .preset(por_1_out));  // open: Qn, reset
  D_Flip_Flop d_ff_2 (.D(Dout[0]), .clk(Clk), .Q(Dout[1]));  // open: Qn, preset, reset
  D_Flip_Flop d_ff_3 (.D(Dout[1]), .clk(Clk), .Q(Dout[2]));  // open: Qn, preset, reset
  D_Flip_Flop d_ff_4 (.D(Dout[2]), .clk(Clk), .Q(Dout[3]));  // open: Qn, preset, reset
  D_Flip_Flop d_ff_5 (.D(Dout[3]), .clk(Clk), .Q(Dout[4]), .Qn(d_ff_5_qn));  // open: preset, reset
  Multiplexer multiplexer_1 (.in0(Dout[4]), .in1(d_ff_5_qn), .out(multiplexer_1_out), .sel(Tipo));
endmodule

module ContadorAscSincModulo10 (
  input  Clk,
  output [3:0] C
);

  wire and_1_out, and_2_out, and_3_out;

  T_Flip_Flop t_ff_1 (.T(1'b1), .clk(Clk), .Q(C[0]), .reset(and_3_out));  // open: Qn, preset
  T_Flip_Flop t_ff_2 (.T(C[0]), .clk(Clk), .Q(C[1]), .reset(and_3_out));  // open: Qn, preset
  and and_1 (and_1_out, C[0], C[1]);
  T_Flip_Flop t_ff_3 (.T(and_1_out), .clk(Clk), .Q(C[2]), .reset(and_3_out));  // open: Qn, preset
  and and_2 (and_2_out, and_1_out, C[2]);
  T_Flip_Flop t_ff_4 (.T(and_2_out), .clk(Clk), .Q(C[3]), .reset(and_3_out));  // open: Qn, preset
  and and_3 (and_3_out, ~C[0], C[1], ~C[2], C[3]);  // AND_Gate
endmodule
