// Logisim project Parcial2u5.circ as structural Verilog
module F01 (
  input  [2:0] A,
  output [3:0] J
);

  wire and_1_out, and_2_out, and_3_out, and_4_out, and_5_out, and_6_out;

  and and_1 (and_1_out, ~A[2], A[1]);  // AND_Gate
  and and_2 (and_2_out, ~A[2], A[0]);  // AND_Gate
  and and_3 (and_3_out, A[2], ~A[1], ~A[0]);  // AND_Gate
  and and_4 (and_4_out, A[2], ~A[1]);  // AND_Gate
  and and_5 (and_5_out, A[2], ~A[0]);  // AND_Gate
  and and_6 (and_6_out, ~A[2], A[1], A[0]);  // AND_Gate
  xor xor_1 (J[1], A[1], A[2]);
  or or_1 (J[0], and_1_out, and_2_out, and_3_out);
  or or_2 (J[2], and_4_out, and_5_out, and_6_out);

  assign J[3] = A[2];
endmodule

module F04 (
  output S
);

  wire clock_1_out;
  wire [2:0] johnson3bits_1_j;

  Clock clock_1 (.out(clock_1_out));
  Johnson3Bits johnson3bits_1 (.Clk(clock_1_out), .J(johnson3bits_1_j));
  Multiplexer #(.select(3)) multiplexer_1 (
    .in0(1'b1), .in1(1'b1), .in2(1'b0), .in3(1'b0), .in4(1'b0), .in5(1'b0), .in6(1'b0), .in7(1'b0), .out(S),
    .sel(johnson3bits_1_j));
endmodule

module Johnson3Bits (
  input  Clk,
  output [2:0] J
);

  wire d_ff_3_qn;

  D_Flip_Flop d_ff_1 (.D(d_ff_3_qn), .clk(Clk), .Q(J[0]));  // open: Qn, preset, reset
  D_Flip_Flop d_ff_2 (.D(J[0]), .clk(Clk), .Q(J[1]));  // open: Qn, preset, reset
  D_Flip_Flop d_ff_3 (.D(J[1]), .clk(Clk), .Q(J[2]), .Qn(d_ff_3_qn));  // open: preset, reset
endmodule

module F08 (
  output [2:0] out_1
);

  wire and_1_out, and_2_out, and_3_out, and_4_out, C0_qn, clock_1_out, or_1_out, or_2_out, or_3_out;

  Clock clock_1 (.out(clock_1_out));
  D_Flip_Flop C0 (.D(C0_qn), .clk(clock_1_out), .Q(out_1[0]), .Qn(C0_qn));  // open: preset, reset
  and and_1 (and_1_out, ~out_1[0], ~out_1[1]);  // AND_Gate
  and and_2 (and_2_out, out_1[0], out_1[1]);
  or or_1 (or_1_out, and_1_out, and_2_out);
  D_Flip_Flop C1 (.D(or_1_out), .clk(clock_1_out), .Q(out_1[1]));  // open: Qn, preset, reset
  and and_3 (and_3_out, out_1[2], or_2_out);
  or or_2 (or_2_out, out_1[0], out_1[1]);
  and and_4 (and_4_out, ~out_1[2], ~out_1[1], ~out_1[0]);  // AND_Gate
  or or_3 (or_3_out, and_3_out, and_4_out);
  D_Flip_Flop C2 (.D(or_3_out), .clk(clock_1_out), .Q(out_1[2]));  // open: Qn, preset, reset

  // Other names for the same wires on the sheet: C0 = out_1[0]; C1 = out_1[1]; C2 = out_1[2]
endmodule

module OneHot5Bits (
  input  Clk,
  output [9:0] out_2
);

  wire por_1_out;

  D_Flip_Flop d_ff_1 (.D(out_2[0]), .clk(Clk), .Q(out_2[9]), .preset(por_1_out));  // open: Qn, reset
  POR por_1 (.out(por_1_out));
  D_Flip_Flop d_ff_2 (.D(out_2[9]), .clk(Clk), .Q(out_2[8]));  // open: Qn, preset, reset
  D_Flip_Flop d_ff_3 (.D(out_2[8]), .clk(Clk), .Q(out_2[7]));  // open: Qn, preset, reset
  D_Flip_Flop d_ff_4 (.D(out_2[7]), .clk(Clk), .Q(out_2[6]));  // open: Qn, preset, reset
  D_Flip_Flop d_ff_5 (.D(out_2[6]), .clk(Clk), .Q(out_2[5]));  // open: Qn, preset, reset
  D_Flip_Flop d_ff_6 (.D(out_2[5]), .clk(Clk), .Q(out_2[4]));  // open: Qn, preset, reset
  D_Flip_Flop d_ff_7 (.D(out_2[4]), .clk(Clk), .Q(out_2[3]));  // open: Qn, preset, reset
  D_Flip_Flop d_ff_8 (.D(out_2[3]), .clk(Clk), .Q(out_2[2]));  // open: Qn, preset, reset
  D_Flip_Flop d_ff_9 (.D(out_2[2]), .clk(Clk), .Q(out_2[1]));  // open: Qn, preset, reset
  D_Flip_Flop d_ff_10 (.D(out_2[1]), .clk(Clk), .Q(out_2[0]));  // open: Qn, preset, reset
endmodule

module F02 (
  output [3:0] BCD
);

  wire clock_1_out;
  wire [9:0] onehot5bits_1_out_2;

  Clock clock_1 (.out(clock_1_out));
  OneHot5Bits onehot5bits_1 (.Clk(clock_1_out), .out_2(onehot5bits_1_out_2));
  or or_1 (BCD[0], onehot5bits_1_out_2[0], onehot5bits_1_out_2[2], onehot5bits_1_out_2[4], onehot5bits_1_out_2[6], onehot5bits_1_out_2[8]);
  or or_2 (BCD[1], onehot5bits_1_out_2[2], onehot5bits_1_out_2[3], onehot5bits_1_out_2[6], onehot5bits_1_out_2[7]);
  or or_3 (BCD[2], onehot5bits_1_out_2[2], onehot5bits_1_out_2[3], onehot5bits_1_out_2[4], onehot5bits_1_out_2[5]);
  or or_4 (BCD[3], onehot5bits_1_out_2[1], onehot5bits_1_out_2[0]);
endmodule

module F05 (
  input  A,
  input  R,
  output F
);

  wire and_1_out, and_2_out, and_3_out, and_4_out, Clk, or_1_out, or_2_out, S0, S1;

  Clock clock_1 (.out(Clk));
  and and_1 (and_1_out, ~S0, A);  // AND_Gate
  and and_2 (and_2_out, ~S1, S0, ~A);  // AND_Gate
  and and_3 (and_3_out, S1, ~A);  // AND_Gate
  and and_4 (and_4_out, ~S1, S0);  // AND_Gate
  D_Flip_Flop d_ff_1 (.D(or_1_out), .clk(Clk), .Q(S0), .reset(R));  // open: Qn, preset
  or or_1 (or_1_out, and_1_out, and_2_out);
  D_Flip_Flop d_ff_2 (.D(or_2_out), .clk(Clk), .Q(S1), .reset(R));  // open: Qn, preset
  or or_2 (or_2_out, and_3_out, and_4_out);
  and and_5 (F, S1, ~S0);  // AND_Gate
endmodule

module F07 (
  input  A0,
  input  A1,
  input  R,
  output F
);

  wire Clk, NS0, NS1, S0, S1;

  Clock clock_1 (.out(Clk));
  ROM #(.addrWidth(4), .dataWidth(3)) rom_1 (.addr({S1, S0, A1, A0}), .data({NS1, NS0, F}));
  D_Flip_Flop d_ff_1 (.D(NS0), .clk(Clk), .Q(S0), .reset(R));  // open: Qn, preset
  D_Flip_Flop d_ff_2 (.D(NS1), .clk(Clk), .Q(S1), .reset(R));  // open: Qn, preset

  // Notes on the sheet:
  //   contents of rom_1 (hex, n*v repeats v):
  //   0 2 4 6 2 4 6 6 4 6 6 6 4*7
endmodule

module FSMF11 (
  input  [3:0] Temp,
  input  Clk,
  input  R,
  output A
);

  wire S;

  ROM #(.addrWidth(5), .dataWidth(1)) rom_1 (.addr({S, Temp}));  // open: data
  D_Flip_Flop d_ff_1 (.D(A), .clk(Clk), .Q(S), .reset(R));  // open: Qn, preset

  // Other names for the same wires on the sheet: NS = A

  // Notes on the sheet:
  //   contents of rom_1 (hex, n*v repeats v):
  //   13*0 1 1 1 8*0 8*1
endmodule

module F11 (
);

  wire clock_1_out, fsmf11_1_a, por_1_out;
  wire [3:0] slider_1_out;

  Clock clock_1 (.out(clock_1_out));
  POR por_1 (.out(por_1_out));
  Slider #(.width(4)) slider_1 (.out(slider_1_out));
  LED led_1 (.in(fsmf11_1_a));
  FSMF11 fsmf11_1 (.Temp(slider_1_out), .Clk(clock_1_out), .R(por_1_out), .A(fsmf11_1_a));
endmodule

module F12 (
);

  wire clock_1_out, multiplexer_1_out, multiplexer_2_out, multiplexer_3_out;
  wire [2:0] Sel;

  Clock clock_1 (.out(clock_1_out));
  Multiplexer #(.select(3)) multiplexer_1 (
    .in0(1'b0), .in1(1'b0), .in2(1'b0), .in3(1'b1), .in4(1'b1), .in5(1'b1), .in6(1'b1), .in7(1'b0),
    .out(multiplexer_1_out), .sel(Sel));
  LED led_1 (.in(Sel[2]));
  D_Flip_Flop d_ff_1 (.D(multiplexer_1_out), .clk(clock_1_out), .Q(Sel[2]));  // open: Qn, preset, reset
  D_Flip_Flop d_ff_2 (.D(multiplexer_2_out), .clk(clock_1_out), .Q(Sel[1]));  // open: Qn, preset, reset
  Multiplexer #(.select(3)) multiplexer_2 (
    .in0(1'b0), .in1(1'b1), .in2(1'b1), .in3(1'b0), .in4(1'b0), .in5(1'b1), .in6(1'b1), .in7(1'b0),
    .out(multiplexer_2_out), .sel(Sel));
  LED led_2 (.in(Sel[1]));
  Multiplexer #(.select(3)) multiplexer_3 (
    .in0(1'b1), .in1(1'b0), .in2(1'b1), .in3(1'b0), .in4(1'b1), .in5(1'b0), .in6(1'b1), .in7(1'b0),
    .out(multiplexer_3_out), .sel(Sel));
  D_Flip_Flop d_ff_3 (.D(multiplexer_3_out), .clk(clock_1_out), .Q(Sel[0]));  // open: Qn, preset, reset
  LED led_3 (.in(Sel[0]));
endmodule

module F13 (
);

  wire clock_1_out, multiplexer_1_out, multiplexer_2_out, multiplexer_3_out;
  wire [2:0] Sel;

  Clock clock_1 (.out(clock_1_out));
  D_Flip_Flop d_ff_1 (.D(multiplexer_1_out), .clk(clock_1_out), .Q(Sel[2]));  // open: Qn, preset, reset
  Multiplexer #(.select(3)) multiplexer_1 (
    .in0(1'b1), .in1(1'b0), .in2(1'b0), .in3(1'b0), .in4(1'b0), .in5(1'b1), .in6(1'b1), .in7(1'b1),
    .out(multiplexer_1_out), .sel(Sel));
  LED led_1 (.in(Sel[2]));
  Multiplexer #(.select(3)) multiplexer_2 (
    .in0(1'b1), .in1(1'b0), .in2(1'b0), .in3(1'b1), .in4(1'b1), .in5(1'b0), .in6(1'b0), .in7(1'b1),
    .out(multiplexer_2_out), .sel(Sel));
  LED led_2 (.in(Sel[1]));
  D_Flip_Flop d_ff_2 (.D(multiplexer_2_out), .clk(clock_1_out), .Q(Sel[1]));  // open: Qn, preset, reset
  D_Flip_Flop d_ff_3 (.D(multiplexer_3_out), .clk(clock_1_out), .Q(Sel[0]));  // open: Qn, preset, reset
  Multiplexer #(.select(3)) multiplexer_3 (
    .in0(1'b1), .in1(1'b0), .in2(1'b1), .in3(1'b0), .in4(1'b1), .in5(1'b0), .in6(1'b1), .in7(1'b0),
    .out(multiplexer_3_out), .sel(Sel));
  LED led_3 (.in(Sel[0]));
endmodule
