// Logisim project Parcialu2.circ as structural Verilog: 1 circuit, main circuit main
module main (
  input  A,
  input  A_2,
  input  B,
  input  B_2,
  input  A_3,
  input  C,
  input  C_2,
  input  B_3,
  input  D,
  input  D_2,
  input  C_3,
  input  A_4,
  input  B_4,
  input  C_4,
  input  A_5,
  input  D_3,
  input  B_5,
  input  C_5,
  input  [3:0] in_19,
  input  A_6,
  input  A_7,
  input  B_6,
  input  B_7,
  input  C_6,
  input  C_7,
  input  D_4,
  input  N3,
  input  D_5,
  input  N2,
  input  N1,
  input  N0,
  output MayorOIgual,
  output F,
  output S,
  output S0,
  output C_8,
  output S1,
  output F_2,
  output S2,
  output S3,
  output S4,
  output F_3,
  output S5,
  output S6,
  output S7,
  output F_4,
  output F_5
);

  wire and_1_out, and_2_out, and_3_out, and_4_out, and_5_out, and_6_out, nand_1_out, nand_3_out, nand_4_out,
       nand_6_out, nand_7_out, nand_8_out, nand_9_out, nand_10_out, nand_11_out, nand_12_out, nor_1_out,
       nor_2_out, nor_3_out, or_10_out, or_11_out;

  nand nand_1 (nand_1_out, ~B_6, ~D_4);  // NAND_Gate
  and and_1 (and_1_out, ~A_4, ~B_4, ~C_4, D_3);  // AND_Gate
  and and_2 (and_2_out, ~A_4, B_4, ~C_4, ~D_3);  // AND_Gate
  and and_3 (and_3_out, ~A_4, B_4, ~C_4, D_3);  // AND_Gate
  and and_4 (and_4_out, ~A_4, B_4, C_4, ~D_3);  // AND_Gate
  and and_5 (and_5_out, A_4, B_4, ~C_4, ~D_3);  // AND_Gate
  and and_6 (and_6_out, A_4, B_4, C_4, ~D_3);  // AND_Gate
  nor nor_1 (nor_1_out, ~A_2, C_2);  // NOR_Gate
  nor nor_2 (nor_2_out, ~A_2, B_2, ~D_2);  // NOR_Gate
  nor nor_3 (nor_3_out, B_2, C_2, ~D_2);  // NOR_Gate
  nand nand_2 (F_4, nand_1_out, nand_1_out);
  nor nor_4 (MayorOIgual, nor_1_out, nor_2_out, nor_3_out);
  or or_1 (F_2, and_1_out, and_2_out, and_3_out, and_4_out, and_5_out, and_6_out);
  nand nand_3 (nand_3_out, B, ~D);  // NAND_Gate
  nand nand_4 (nand_4_out, ~A, ~C, D);  // NAND_Gate
  or or_2 (S0, A_5, B_5, C_5);
  or or_3 (S1, A_5, B_5, ~C_5);  // OR_Gate
  or or_4 (S2, A_5, ~B_5, C_5);  // OR_Gate
  or or_5 (S3, A_5, ~B_5, ~C_5);  // OR_Gate
  or or_6 (S4, ~A_5, B_5, C_5);  // OR_Gate
  or or_7 (S5, ~A_5, B_5, ~C_5);  // OR_Gate
  or or_8 (S6, ~A_5, ~B_5, C_5);  // OR_Gate
  or or_9 (S7, ~A_5, ~B_5, ~C_5);  // OR_Gate
  buf or_10 (or_10_out, N3);  // OR_Gate
  or or_11 (or_11_out, N2, N1);
  nand nand_5 (F, nand_3_out, nand_4_out);
  and and_7 (F_5, or_10_out, or_11_out);
  Multiplexer #(.select(4), .enable("false")) multiplexer_1 (
    .in0(1'b0), .in1(1'b1), .in2(1'b0), .in3(1'b1), .in4(1'b0), .in5(1'b0), .in6(1'b0), .in7(1'b1),
    .in8(1'b0), .in9(1'b1), .in10(1'b0), .in11(1'b1), .in12(1'b1), .in13(1'b0), .in14(1'b0), .in15(1'b0),
    .out(F_3), .sel(in_19));
  nand nand_6 (nand_6_out, A_3, ~B_3, ~C_3);  // NAND_Gate
  nand nand_7 (nand_7_out, ~A_3, B_3, ~C_3);  // NAND_Gate
  nand nand_8 (nand_8_out, ~A_3, ~B_3, C_3);  // NAND_Gate
  nand nand_9 (nand_9_out, A_3, B_3, C_3);
  nand nand_10 (nand_10_out, A_3, B_3);
  nand nand_11 (nand_11_out, A_3, C_3);
  nand nand_12 (nand_12_out, B_3, C_3);
  nand nand_13 (S, nand_6_out, nand_7_out, nand_8_out, nand_9_out);
  nand nand_14 (C_8, nand_10_out, nand_11_out, nand_12_out);

  // Other names for the same wires on the sheet: A_t = A_5; B_t = B_5; C_t = C_5
endmodule
