// Logisim project SemaforoProgramable.circ as structural Verilog: 2 circuits, main circuit main
module main (
);

  wire and_1_out, and_2_out, and_3_out, and_4_out, Clk, CLR, not_1_out, NS0, NS1, Reset, S0, S1, T0, T1, T2,
       T3;

  LED R1 (.in(S1));
  and and_1 (and_1_out, ~S1, S0);  // AND_Gate
  LED A1 (.in(and_1_out));
  and and_2 (and_2_out, ~S1, ~S0);  // AND_Gate
  LED V1 (.in(and_2_out));
  not not_1 (not_1_out, S1);
  LED R2 (.in(not_1_out));
  and and_3 (and_3_out, S0, S1);
  LED A2 (.in(and_3_out));
  and and_4 (and_4_out, ~S0, S1);  // AND_Gate
  LED V2 (.in(and_4_out));
  Clock clock_1 (.out(Clk));
  Hex_Digit_Display hex_digit_display_1 (.value({T3, T2, T1, T0}));  // open: dp
  Contador contador_1 (.Clk(Clk), .CLR(CLR), .Reset(Reset), .T0(T0), .T1(T1), .T2(T2), .T3(T3));
  POR por_1 (.out(Reset));
  ROM #(.addrWidth(6), .dataWidth(3)) rom_1 (.addr({S1, S0, T3, T2, T1, T0}), .data({CLR, NS1, NS0}));
  D_Flip_Flop u_S0 (.D(NS0), .clk(Clk), .Q(S0), .reset(Reset));  // open: Qn, preset
  D_Flip_Flop u_S1 (.D(NS1), .clk(Clk), .Q(S1), .reset(Reset));  // open: Qn, preset

  // Notes on the sheet:
  //   contents of rom_1 (hex, n*v repeats v):
  //   11*0 5 4*0 4*1 6 11*0 13*2 7 0 0 3 4
endmodule

module Contador (
  input  Clk,
  input  CLR,
  input  Reset,
  output T0,
  output T1,
  output T2,
  output T3
);

  wire and_1_out, and_2_out, and_3_out, and_4_out, and_5_out, and_6_out, xor_1_out, xor_2_out, xor_3_out;

  D_Flip_Flop d_ff_1 (.D(and_1_out), .clk(Clk), .Q(T0), .reset(Reset));  // open: Qn, preset
  and and_1 (and_1_out, ~T0, ~CLR);  // AND_Gate
  xor xor_1 (xor_1_out, T1, T0);
  and and_2 (and_2_out, xor_1_out, ~CLR);  // AND_Gate
  D_Flip_Flop d_ff_2 (.D(and_2_out), .clk(Clk), .Q(T1), .reset(Reset));  // open: Qn, preset
  and and_3 (and_3_out, T0, T1);
  xor xor_2 (xor_2_out, T2, and_3_out);
  and and_4 (and_4_out, xor_2_out, ~CLR);  // AND_Gate
  D_Flip_Flop d_ff_3 (.D(and_4_out), .clk(Clk), .Q(T2), .reset(Reset));  // open: Qn, preset
  xor xor_3 (xor_3_out, T3, and_5_out);
  and and_5 (and_5_out, T2, and_3_out);
  D_Flip_Flop d_ff_4 (.D(and_6_out), .clk(Clk), .Q(T3), .reset(Reset));  // open: Qn, preset
  and and_6 (and_6_out, xor_3_out, ~CLR);  // AND_Gate
endmodule
