// Logisim project TPu2.circ as structural Verilog: 38 circuits, main circuit main
module main (
  input  E1,
  input  E2,
  input  [3:0] A,
  input  [3:0] A_2,
  input  E3,
  input  [3:0] B,
  input  E4,
  input  [2:0] Seleccion,
  input  E5,
  input  E6,
  input  [3:0] B_2,
  input  E7,
  input  E8,
  input  E9,
  input  E10,
  input  E11,
  input  E12,
  input  E13,
  input  [3:0] A_3,
  input  E14,
  input  E15,
  input  [3:0] B_3,
  input  [3:0] A_4,
  input  [3:0] A_5,
  input  [3:0] A_6,
  input  [3:0] B_4,
  input  [3:0] B_5,
  input  [3:0] B_6,
  input  [1:0] A_7,
  input  [1:0] B_7,
  output [3:0] BCD0,
  output [3:0] BCD1,
  output [3:0] F,
  output [3:0] S,
  output [3:0] R,
  output [3:0] R_2,
  output [3:0] M
);

  wire alu_1_borrow, alu_1_carry, comparador_1_aeqb, comparador_1_agtbsigned, comparador_1_agtbunsigned,
       comparador_1_agtebsigned, comparador_1_agtebunsigned, comparador_1_altbsigned,
       comparador_1_altbunsigned, comparador_1_altebsigned, comparador_1_altebunsigned, comparador_1_aneqb,
       compbasenegativos_1_signo, compbasenegativos_2_signo, compbasenegativos_3_signo, conversor7seg_1_sa,
       conversor7seg_1_sb, conversor7seg_1_sc, conversor7seg_1_sd, conversor7seg_1_se, conversor7seg_1_sf,
       conversor7seg_1_sg, encodersimple_1_a, encodersimple_1_b, encodersimple_1_c, encodersimple_1_d,
       restadorsignado4bits_1_cout, restadorsinsigno4bits_1_bout, sumador4bits_1_cout;
  wire [3:0] compbasenegativos_1_f, compbasenegativos_2_f, compbasenegativos_3_f;

  Hex_Digit_Display hex_digit_display_1 (.value(A_6));  // open: dp
  Hex_Digit_Display hex_digit_display_2 (.value(B_6));  // open: dp
  RestadorSinSigno4Bits restadorsinsigno4bits_1 (.A(A_6), .B(B_6), .R(R_2), .Bout(restadorsinsigno4bits_1_bout));
  Hex_Digit_Display hex_digit_display_3 (.value(R_2));  // open: dp
  LED Bout (.in(restadorsinsigno4bits_1_bout));
  EncoderSimple encodersimple_1 (
    .E1(E1), .E2(E2), .E3(E3), .E4(E4), .E5(E5), .E6(E6), .E7(E7), .E8(E8), .E9(E9), .E10(E10), .E11(E11),
    .E12(E12), .E13(E13), .E14(E14), .E15(E15), .A(encodersimple_1_a), .B(encodersimple_1_b),
    .C(encodersimple_1_c), .D(encodersimple_1_d));
  _7_Segment_Display u_7_segment_display_1 (.g(compbasenegativos_1_signo));  // open: f, a, b, e, d, c, dp
  CompBaseNegativos compbasenegativos_1 (.A(R_2), .F(compbasenegativos_1_f), .Signo(compbasenegativos_1_signo));
  Conversor7Seg conversor7seg_1 (
    .A(encodersimple_1_a), .B(encodersimple_1_b), .C(encodersimple_1_c), .D(encodersimple_1_d),
    .SA(conversor7seg_1_sa), .SB(conversor7seg_1_sb), .SC(conversor7seg_1_sc), .SD(conversor7seg_1_sd),
    .SE(conversor7seg_1_se), .SF(conversor7seg_1_sf), .SG(conversor7seg_1_sg));
  Hex_Digit_Display hex_digit_display_4 (.value(compbasenegativos_1_f));  // open: dp
  _7_Segment_Display u_7_segment_display_2 (
    .g(conversor7seg_1_sg), .f(conversor7seg_1_sf), .a(conversor7seg_1_sa), .b(conversor7seg_1_sb),
    .e(conversor7seg_1_se), .d(conversor7seg_1_sd), .c(conversor7seg_1_sc));  // open: dp
  Hex_Digit_Display hex_digit_display_5 (.value(A));  // open: dp
  Hex_Digit_Display hex_digit_display_6 (.value(B_2));  // open: dp
  Hex_Digit_Display hex_digit_display_7 (.value(A_3));  // open: dp
  Hex_Digit_Display hex_digit_display_8 (.value(B_3));  // open: dp
  SumadorBCD sumadorbcd_1 (.A(A), .B(B_2), .BCD0(BCD0), .BCD1(BCD1));
  Sumador4Bits sumador4bits_1 (.A(A_3), .B(B_3), .S(S), .Cout(sumador4bits_1_cout));
  Comparador comparador_1 (
    .A(A_5), .B(B_4), .AeqB(comparador_1_aeqb), .AneqB(comparador_1_aneqb),
    .AgtBsigned(comparador_1_agtbsigned), .AgteBsigned(comparador_1_agtebsigned),
    .AltBsigned(comparador_1_altbsigned), .AlteBsigned(comparador_1_altebsigned),
    .AgteBunsigned(comparador_1_agtebunsigned), .AgtBunsigned(comparador_1_agtbunsigned),
    .AltBunsigned(comparador_1_altbunsigned), .AlteBunsigned(comparador_1_altebunsigned));
  Hex_Digit_Display hex_digit_display_9 (.value(BCD1));  // open: dp
  Hex_Digit_Display hex_digit_display_10 (.value(S));  // open: dp
  LED Cout (.in(sumador4bits_1_cout));
  LED AeqB (.in(comparador_1_aeqb));
  LED AneqB (.in(comparador_1_aneqb));
  LED AgteBsigned (.in(comparador_1_agtebsigned));
  LED AgtBsigned (.in(comparador_1_agtbsigned));
  LED AlteBsigned (.in(comparador_1_altebsigned));
  LED AltBsigned (.in(comparador_1_altbsigned));
  LED AgteBunsigned (.in(comparador_1_agtebunsigned));
  LED AgtBunsigned (.in(comparador_1_agtbunsigned));
  LED AlteBunsigned (.in(comparador_1_altebunsigned));
  LED AltBunsigned (.in(comparador_1_altbunsigned));
  Hex_Digit_Display hex_digit_display_11 (.value(BCD0));  // open: dp
  Hex_Digit_Display hex_digit_display_12 (.value(A_4));  // open: dp
  Hex_Digit_Display hex_digit_display_13 (.value(B_5));  // open: dp
  ALU alu_1 (.A(A_2), .B(B), .Seleccion(Seleccion), .Borrow(alu_1_borrow), .Carry(alu_1_carry), .F(F));
  Hex_Digit_Display hex_digit_display_14 (.value(R));  // open: dp
  RestadorSignado4Bits restadorsignado4bits_1 (.A(A_4), .B(B_5), .R(R), .Cout(restadorsignado4bits_1_cout));
  Hex_Digit_Display hex_digit_display_15 (.value(M));  // open: dp
  D20 d20_1 (.A(A_7), .B(B_7), .M(M));
  LED Borrow (.in(alu_1_borrow));
  LED Carry (.in(alu_1_carry));
  LED Cout_2 (.in(restadorsignado4bits_1_cout));
  _7_Segment_Display u_7_segment_display_3 (.g(compbasenegativos_2_signo));  // open: f, a, b, e, d, c, dp
  CompBaseNegativos compbasenegativos_2 (.A(M), .F(compbasenegativos_2_f), .Signo(compbasenegativos_2_signo));
  _7_Segment_Display u_7_segment_display_4 (.g(compbasenegativos_3_signo));  // open: f, a, b, e, d, c, dp
  CompBaseNegativos compbasenegativos_3 (.A(R), .F(compbasenegativos_3_f), .Signo(compbasenegativos_3_signo));
  Hex_Digit_Display hex_digit_display_16 (.value(compbasenegativos_2_f));  // open: dp
  Hex_Digit_Display hex_digit_display_17 (.value(compbasenegativos_3_f));  // open: dp
endmodule

module FD03 (
  input  A,
  input  B,
  input  D
);

  wire nand_1_out, nand_2_out, nand_3_out;

  nand nand_1 (nand_1_out, ~A, B);  // NAND_Gate
  nand nand_2 (nand_2_out, B, ~D);  // NAND_Gate
  nand nand_3 (nand_3_out, nand_1_out, nand_2_out);
  LED led_1 (.in(nand_3_out));
endmodule

module FD04 (
  input  A,
  input  D,
  input  B
);

  wire nor_1_out, nor_2_out, nor_3_out;

  nor nor_1 (nor_1_out, ~A, ~D);  // NOR_Gate
  nor nor_2 (nor_2_out, B, B);
  LED led_1 (.in(nor_3_out));
  nor nor_3 (nor_3_out, nor_1_out, nor_2_out);
endmodule

module FD05 (
  input  [3:0] in_1
);

  wire multiplexer_1_out;

  Multiplexer #(.select(4), .enable("false")) multiplexer_1 (
    .in0(1'b0), .in1(1'b0), .in2(1'b0), .in3(1'b0), .in4(1'b1), .in5(1'b1), .in6(1'b1), .in7(1'b0),
    .in8(1'b0), .in9(1'b0), .in10(1'b0), .in11(1'b0), .in12(1'b1), .in13(1'b0), .in14(1'b1), .in15(1'b0),
    .out(multiplexer_1_out), .sel(in_1));
  LED led_1 (.in(multiplexer_1_out));
endmodule

module FA07 (
  input  [3:0] ABCD,
  output out_2
);

  wire nand_1_out, nand_2_out, nand_3_out, nand_4_out, nand_5_out, nand_6_out;

  nand nand_1 (nand_1_out, ~ABCD[3], ABCD[1]);  // NAND_Gate
  nand nand_2 (nand_2_out, ABCD[3], ~ABCD[0]);  // NAND_Gate
  nand nand_3 (nand_3_out, ABCD[2], ABCD[1]);
  nand nand_4 (nand_4_out, ~ABCD[3], ABCD[2], ABCD[0]);  // NAND_Gate
  nand nand_5 (nand_5_out, ABCD[3], ~ABCD[2], ~ABCD[1]);  // NAND_Gate
  nand nand_6 (nand_6_out, ~ABCD[2], ~ABCD[0]);  // NAND_Gate
  nand nand_7 (out_2, nand_1_out, nand_2_out, nand_3_out, nand_4_out, nand_5_out, nand_6_out);
endmodule

module FB07 (
  input  [3:0] ABCD,
  output out_2
);

  wire nand_1_out, nand_2_out, nand_3_out, nand_4_out, nand_5_out;

  nand nand_1 (nand_1_out, ~ABCD[2], ~ABCD[1]);  // NAND_Gate
  nand nand_2 (nand_2_out, ~ABCD[2], ~ABCD[0]);  // NAND_Gate
  nand nand_3 (nand_3_out, ~ABCD[3], ABCD[1], ABCD[0]);  // NAND_Gate
  nand nand_4 (nand_4_out, ABCD[3], ~ABCD[1], ABCD[0]);  // NAND_Gate
  nand nand_5 (nand_5_out, ~ABCD[3], ~ABCD[1], ~ABCD[0]);  // NAND_Gate
  nand nand_6 (out_2, nand_1_out, nand_2_out, nand_3_out, nand_4_out, nand_5_out);
endmodule

module FC07 (
  input  [3:0] ABCD,
  output out_2
);

  wire nand_1_out, nand_2_out, nand_3_out, nand_4_out, nand_5_out;

  nand nand_1 (nand_1_out, ~ABCD[3], ABCD[2]);  // NAND_Gate
  nand nand_2 (nand_2_out, ABCD[3], ~ABCD[2]);  // NAND_Gate
  nand nand_3 (nand_3_out, ~ABCD[1], ABCD[0]);  // NAND_Gate
  nand nand_4 (nand_4_out, ~ABCD[3], ABCD[0]);  // NAND_Gate
  nand nand_5 (nand_5_out, ~ABCD[2], ~ABCD[1]);  // NAND_Gate
  nand nand_6 (out_2, nand_1_out, nand_2_out, nand_3_out, nand_4_out, nand_5_out);
endmodule

module FD07 (
  input  [3:0] ABCD,
  output out_2
);

  wire nand_1_out, nand_2_out, nand_3_out, nand_4_out, nand_5_out;

  nand nand_1 (nand_1_out, ABCD[3], ~ABCD[1]);  // NAND_Gate
  nand nand_2 (nand_2_out, ABCD[2], ~ABCD[1], ABCD[0]);  // NAND_Gate
  nand nand_3 (nand_3_out, ~ABCD[3], ~ABCD[2], ~ABCD[0]);  // NAND_Gate
  nand nand_4 (nand_4_out, ~ABCD[2], ABCD[1], ABCD[0]);  // NAND_Gate
  nand nand_5 (nand_5_out, ABCD[2], ABCD[1], ~ABCD[0]);  // NAND_Gate
  nand nand_6 (out_2, nand_1_out, nand_2_out, nand_3_out, nand_4_out, nand_5_out);
endmodule

module FE07 (
  input  [3:0] ABCD,
  output out_2
);

  Multiplexer #(.select(4), .enable("false")) multiplexer_1 (
    .in0(1'b1), .in1(1'b0), .in2(1'b1), .in3(1'b0), .in4(1'b0), .in5(1'b0), .in6(1'b1), .in7(1'b0),
    .in8(1'b1), .in9(1'b0), .in10(1'b1), .in11(1'b1), .in12(1'b1), .in13(1'b1), .in14(1'b1), .in15(1'b1),
    .out(out_2), .sel(ABCD));
endmodule

module FF07 (
  input  [3:0] ABCD,
  output out_2
);

  wire nor_1_out, nor_2_out, nor_3_out, nor_4_out;

  nor nor_1 (nor_1_out, ABCD[3], ABCD[2], ~ABCD[0]);  // NOR_Gate
  nor nor_2 (nor_2_out, ABCD[3], ABCD[2], ~ABCD[1]);  // NOR_Gate
  nor nor_3 (nor_3_out, ABCD[3], ~ABCD[1], ~ABCD[0]);  // NOR_Gate
  nor nor_4 (nor_4_out, ~ABCD[3], ~ABCD[2], ABCD[1], ~ABCD[0]);  // NOR_Gate
  nor nor_5 (out_2, nor_1_out, nor_2_out, nor_3_out, nor_4_out);
endmodule

module FG07 (
  input  [3:0] ABCD,
  output out_2
);

  wire nor_1_out, nor_2_out, nor_3_out;

  nor nor_1 (nor_1_out, ABCD[3], ABCD[2], ABCD[1]);
  nor nor_2 (nor_2_out, ABCD[3], ~ABCD[2], ~ABCD[1], ~ABCD[0]);  // NOR_Gate
  nor nor_3 (nor_3_out, ~ABCD[3], ~ABCD[2], ABCD[1], ABCD[0]);  // NOR_Gate
  nor nor_4 (out_2, nor_1_out, nor_2_out, nor_3_out);
endmodule

module Conversor7Seg (
  input  A,
  input  B,
  input  C,
  input  D,
  output SA,
  output SB,
  output SC,
  output SD,
  output SE,
  output SF,
  output SG
);

  FA07 FA07 (.ABCD({A, B, C, D}), .out_2(SA));
  FB07 FB07 (.ABCD({A, B, C, D}), .out_2(SB));
  FC07 FC07 (.ABCD({A, B, C, D}), .out_2(SC));
  FD07 FD07 (.ABCD({A, B, C, D}), .out_2(SD));
  FE07 FE07 (.ABCD({A, B, C, D}), .out_2(SE));
  FF07 FF07 (.ABCD({A, B, C, D}), .out_2(SF));
  FG07 FG07 (.ABCD({A, B, C, D}), .out_2(SG));
endmodule

module EncoderSimple (
  input  E1,
  input  E2,
  input  E3,
  input  E4,
  input  E5,
  input  E6,
  input  E7,
  input  E8,
  input  E9,
  input  E10,
  input  E11,
  input  E12,
  input  E13,
  input  E14,
  input  E15,
  output A,
  output B,
  output C,
  output D
);

  or or_1 (D, E1, E3, E5, E7, E9, E11, E13, E15);
  or or_2 (C, E2, E3, E6, E7, E10, E11, E14, E15);
  or or_3 (B, E4, E5, E6, E7, E12, E13, E14, E15);
  or or_4 (A, E8, E9, E10, E11, E12, E13, E14, E15);
endmodule

module Sumador4Bits (
  input  [3:0] A,
  input  [3:0] B,
  output [3:0] S,
  output Cout
);

  wire fulladder_1_cout, fulladder_2_cout, fulladder_3_cout;

  FullAdder fulladder_1 (.A(A[0]), .B(B[0]), .S(S[0]), .Cout(fulladder_1_cout));  // open: Cin
  FullAdder fulladder_2 (.A(fulladder_1_cout), .B(A[1]), .Cin(B[1]), .S(S[1]), .Cout(fulladder_2_cout));
  FullAdder fulladder_3 (.A(fulladder_2_cout), .B(A[2]), .Cin(B[2]), .S(S[2]), .Cout(fulladder_3_cout));
  FullAdder fulladder_4 (.A(fulladder_3_cout), .B(A[3]), .Cin(B[3]), .S(S[3]), .Cout(Cout));
endmodule

module FullAdder (
  input  A,
  input  B,
  input  Cin,
  output S,
  output Cout
);

  wire and_1_out, and_2_out, and_3_out, xor_1_out;

  and and_1 (and_1_out, A, B);
  and and_2 (and_2_out, A, Cin);
  and and_3 (and_3_out, B, Cin);
  xor xor_1 (xor_1_out, A, B);
  xor xor_2 (S, xor_1_out, Cin);
  or or_1 (Cout, and_1_out, and_2_out, and_3_out);
endmodule

module SumadorBCD (
  input  [3:0] A,
  input  [3:0] B,
  output [3:0] BCD0,
  output [3:0] BCD1
);

  wire fuerarangobcd_1_f, or_1_out, sumador4bits_1_cout, sumador4bits_2_cout;
  wire [3:0] sumador4bits_1_s, sumador4bits_2_s;

  Sumador4Bits sumador4bits_1 (.A(A), .B(B), .S(sumador4bits_1_s), .Cout(sumador4bits_1_cout));
  FueraRangoBCD fuerarangobcd_1 (
    .S1(sumador4bits_1_s[3]), .S2(sumador4bits_1_s[2]), .S3(sumador4bits_1_s[1]), .S4(sumador4bits_1_s[0]),
    .F(fuerarangobcd_1_f));
  Sumador4Bits sumador4bits_2 (.A(4'b0110), .B(sumador4bits_1_s), .S(sumador4bits_2_s), .Cout(sumador4bits_2_cout));
  or or_1 (or_1_out, fuerarangobcd_1_f, sumador4bits_1_cout);
  Multiplexer #(.width(4), .enable("false")) multiplexer_1 (
    .in0(sumador4bits_1_s), .in1(sumador4bits_2_s), .out(BCD0), .sel(or_1_out));
  or or_2 (BCD1[0], sumador4bits_2_cout, sumador4bits_1_cout);

  assign BCD1[3:1] = 3'b000;
endmodule

module Mayoria (
  input  A,
  input  B,
  input  C,
  output F
);

  wire and_1_out, and_2_out, and_3_out;

  and and_1 (and_1_out, A, B);
  and and_2 (and_2_out, A, C);
  and and_3 (and_3_out, B, C);
  or or_1 (F, and_1_out, and_2_out, and_3_out);
endmodule

module FueraRangoBCD (
  input  S1,
  input  S2,
  input  S3,
  input  S4,
  output F
);

  wire and_1_out, and_2_out;

  and and_1 (and_1_out, S1, S2);
  and and_2 (and_2_out, S1, S3);
  or or_1 (F, and_1_out, and_2_out);
endmodule

module CompBase (
  input  [3:0] A,
  output [3:0] F,
  output Signo
);

  wire [3:0] not_1_out;

  not not_1 (not_1_out[0], A[0]);
  not not_2 (not_1_out[1], A[1]);
  not not_3 (not_1_out[2], A[2]);
  not not_4 (not_1_out[3], A[3]);
  Sumador4Bits sumador4bits_1 (.A(not_1_out), .B(4'b0001), .S(F));  // open: Cout

  assign Signo = A[3];
endmodule

module Substracter (
  input  Bin,
  input  A,
  input  B,
  output R,
  output Bout
);

  wire and_1_out, and_2_out, and_3_out, xor_1_out;

  xor xor_1 (xor_1_out, B, Bin);
  and and_1 (and_1_out, ~A, Bin);  // AND_Gate
  and and_2 (and_2_out, ~A, B);  // AND_Gate
  and and_3 (and_3_out, B, Bin);
  xor xor_2 (R, A, xor_1_out);
  or or_1 (Bout, and_1_out, and_2_out, and_3_out);
endmodule

module RestadorSinSigno4Bits (
  input  [3:0] A,
  input  [3:0] B,
  output [3:0] R,
  output Bout
);

  wire substracter_1_bout, substracter_2_bout, substracter_3_bout;

  Substracter substracter_1 (.Bin(1'b0), .A(A[0]), .B(B[0]), .R(R[0]), .Bout(substracter_1_bout));
  Substracter substracter_2 (.Bin(substracter_1_bout), .A(A[1]), .B(B[1]), .R(R[1]), .Bout(substracter_2_bout));
  Substracter substracter_3 (.Bin(substracter_2_bout), .A(A[2]), .B(B[2]), .R(R[2]), .Bout(substracter_3_bout));
  Substracter substracter_4 (.Bin(substracter_3_bout), .A(A[3]), .B(B[3]), .R(R[3]), .Bout(Bout));
endmodule

module RestadorSignado4Bits (
  input  [3:0] A,
  input  [3:0] B,
  output [3:0] R,
  output Cout
);

  wire [3:0] compbase_1_f;

  CompBase compbase_1 (.A(B), .F(compbase_1_f));  // open: Signo
  Sumador4Bits sumador4bits_1 (.A(A), .B(compbase_1_f), .S(R), .Cout(Cout));
endmodule

module CompBaseV2 (
  input  [3:0] A,
  output [3:0] F,
  output Signo
);

  RestadorSinSigno4Bits restadorsinsigno4bits_1 (.A(4'b0000), .B(A), .R(F));  // open: Bout

  assign Signo = F[3];
endmodule

module Comparador (
  input  [3:0] A,
  input  [3:0] B,
  output AeqB,
  output AneqB,
  output AgtBsigned,
  output AgteBsigned,
  output AltBsigned,
  output AlteBsigned,
  output AgteBunsigned,
  output AgtBunsigned,
  output AltBunsigned,
  output AlteBunsigned
);

  wire overflow_1_v;
  wire [3:0] restadorsinsigno4bits_1_r;

  RestadorSinSigno4Bits restadorsinsigno4bits_1 (.A(A), .B(B), .R(restadorsinsigno4bits_1_r), .Bout(AltBunsigned));
  nor nor_1 (AeqB, restadorsinsigno4bits_1_r[0], restadorsinsigno4bits_1_r[1], restadorsinsigno4bits_1_r[2], restadorsinsigno4bits_1_r[3]);
  or or_1 (AneqB, restadorsinsigno4bits_1_r[0], restadorsinsigno4bits_1_r[1], restadorsinsigno4bits_1_r[2], restadorsinsigno4bits_1_r[3]);
  Overflow overflow_1 (.A3(A[3]), .B3(B[3]), .R3(restadorsinsigno4bits_1_r[3]), .V(overflow_1_v));
  not not_1 (AgteBunsigned, AltBunsigned);
  xnor xnor_1 (AgteBsigned, overflow_1_v, restadorsinsigno4bits_1_r[3]);
  xor xor_1 (AltBsigned, overflow_1_v, restadorsinsigno4bits_1_r[3]);
  xor xor_2 (AgtBsigned, AgteBsigned, AeqB);
  or or_2 (AlteBsigned, AeqB, AltBsigned);
  xor xor_3 (AgtBunsigned, AgteBunsigned, AeqB);
  or or_3 (AlteBunsigned, AeqB, AltBunsigned);
endmodule

module Overflow (
  input  A3,
  input  B3,
  input  R3,
  output V
);

  wire and_1_out, and_2_out;

  and and_1 (and_1_out, ~A3, B3, R3);  // AND_Gate
  and and_2 (and_2_out, A3, ~B3, ~R3);  // AND_Gate
  or or_1 (V, and_1_out, and_2_out);
endmodule

module CompBaseNegativos (
  input  [3:0] A,
  output [3:0] F,
  output Signo
);

  wire [3:0] not_1_out, sumador4bits_1_s;

  not not_1 (not_1_out[0], A[0]);
  not not_2 (not_1_out[1], A[1]);
  not not_3 (not_1_out[2], A[2]);
  not not_4 (not_1_out[3], A[3]);
  Sumador4Bits sumador4bits_1 (.A(not_1_out), .B(4'b0001), .S(sumador4bits_1_s));  // open: Cout
  Multiplexer #(.width(4), .enable("false")) multiplexer_1 (.in0(A), .in1(sumador4bits_1_s), .out(F), .sel(A[3]));

  assign Signo = A[3];
endmodule

module DesplazaDerechaLogico (
  input  [3:0] Dato,
  input  [1:0] Cantidad,
  output [3:0] F
);

  Multiplexer #(.select(2), .width(4), .enable("false")) multiplexer_1 (
    .in0(Dato), .in1({1'b0, Dato[3:1]}), .in2({2'b00, Dato[3:2]}), .in3({3'b000, Dato[3]}), .out(F),
    .sel(Cantidad));
endmodule

module DesplazaDerechaAritmetico (
  input  [3:0] Dato,
  input  [1:0] Cantidad,
  output [3:0] F
);

  Multiplexer #(.select(2), .width(4), .enable("false")) multiplexer_1 (
    .in0(Dato), .in1({{2{Dato[3]}}, Dato[2:1]}), .in2({{3{Dato[3]}}, Dato[2]}), .in3({4{Dato[3]}}), .out(F),
    .sel(Cantidad));
endmodule

module DesplazaIzquierda (
  input  [3:0] Dato,
  input  [1:0] Cantidad,
  output [3:0] F
);

  Multiplexer #(.select(2), .width(4), .enable("false")) multiplexer_1 (
    .in0(Dato), .in1({Dato[2:0], 1'b0}), .in2({Dato[1:0], 2'b00}), .in3({Dato[0], 3'b000}), .out(F),
    .sel(Cantidad));
endmodule

module AndBitwise (
  input  [3:0] A,
  input  [3:0] B,
  output [3:0] F
);

  and and_1 (F[0], A[0], B[0]);
  and and_2 (F[1], A[1], B[1]);
  and and_3 (F[2], A[2], B[2]);
  and and_4 (F[3], A[3], B[3]);
endmodule

module ALU (
  input  [3:0] A,
  input  [3:0] B,
  input  [2:0] Seleccion,
  output Borrow,
  output Carry,
  output [3:0] F
);

  wire [3:0] andbitwise_1_f, compbasev2_1_f, compbasev2_2_f, desplazaderechaaritmetico_1_f,
       desplazaderechalogico_1_f, desplazaizquierda_1_f, restadorsinsigno4bits_1_r, sumador4bits_1_s;

  RestadorSinSigno4Bits restadorsinsigno4bits_1 (.A(A), .B(B), .R(restadorsinsigno4bits_1_r), .Bout(Borrow));
  Sumador4Bits sumador4bits_1 (.A(A), .B(B), .S(sumador4bits_1_s), .Cout(Carry));
  CompBaseV2 compbasev2_1 (.A(A), .F(compbasev2_1_f));  // open: Signo
  CompBaseV2 compbasev2_2 (.A(B), .F(compbasev2_2_f));  // open: Signo
  DesplazaDerechaLogico desplazaderechalogico_1 (.Dato(A), .Cantidad(B[1:0]), .F(desplazaderechalogico_1_f));
  DesplazaDerechaAritmetico desplazaderechaaritmetico_1 (
    .Dato(A), .Cantidad(B[1:0]), .F(desplazaderechaaritmetico_1_f));
  DesplazaIzquierda desplazaizquierda_1 (.Dato(A), .Cantidad(B[1:0]), .F(desplazaizquierda_1_f));
  AndBitwise andbitwise_1 (.A(A), .B(B), .F(andbitwise_1_f));
  Multiplexer #(.select(3), .width(4), .enable("false")) multiplexer_1 (
    .in0(restadorsinsigno4bits_1_r), .in1(sumador4bits_1_s), .in2(compbasev2_1_f), .in3(compbasev2_2_f),
    .in4(desplazaderechalogico_1_f), .in5(desplazaderechaaritmetico_1_f), .in6(desplazaizquierda_1_f),
    .in7(andbitwise_1_f), .out(F), .sel(Seleccion));
endmodule

module D19 (
  input  [1:0] A,
  input  [1:0] B,
  output [3:0] A_2
);

  wire nand_1_out, nand_2_out, nand_3_out, nand_4_out, nand_5_out, nand_6_out, nand_7_out, nand_8_out,
       nand_9_out;

  nand nand_1 (nand_1_out, ~A[0], B[0]);  // NAND_Gate
  nand nand_2 (nand_2_out, A[0], ~B[0]);  // NAND_Gate
  nand nand_3 (nand_3_out, ~A[0], A[1], ~B[1]);  // NAND_Gate
  nand nand_4 (nand_4_out, A[1], ~B[1], ~B[0]);  // NAND_Gate
  nand nand_5 (nand_5_out, ~A[0], ~A[1], B[1]);  // NAND_Gate
  nand nand_6 (nand_6_out, ~A[1], B[1], ~B[0]);  // NAND_Gate
  nand nand_7 (nand_7_out, ~A[1], A[0], B[0], ~B[1]);  // NAND_Gate
  nand nand_8 (nand_8_out, A[1], A[0], B[1], B[0]);
  nand nand_9 (nand_9_out, A[1], A[0], ~B[1], B[0]);  // NAND_Gate
  nand nand_10 (A_2[0], nand_1_out, nand_2_out);
  nand nand_11 (A_2[1], nand_3_out, nand_4_out, nand_5_out, nand_6_out, nand_7_out, nand_8_out);
  nand nand_12 (A_2[2], nand_5_out, nand_6_out, nand_9_out);
  nand nand_13 (A_2[3], nand_5_out, nand_6_out);
endmodule

module D20 (
  input  [1:0] A,
  input  [1:0] B,
  output [3:0] M
);

  wire nand_1_out, nand_2_out, nand_3_out, nand_4_out, nand_5_out, nand_6_out, nand_7_out, nand_8_out;

  nand nand_1 (nand_1_out, A[0], B[0]);
  nand nand_2 (nand_2_out, A[1], ~A[0], B[0]);  // NAND_Gate
  nand nand_3 (nand_3_out, A[1], ~B[1], B[0]);  // NAND_Gate
  nand nand_4 (nand_4_out, ~A[1], A[0], B[1]);  // NAND_Gate
  nand nand_5 (nand_5_out, A[0], B[1], ~B[0]);  // NAND_Gate
  nand nand_6 (nand_6_out, A[1], B[1], B[0]);
  nand nand_7 (nand_7_out, A[1], ~A[0], B[1]);  // NAND_Gate
  nand nand_8 (nand_8_out, A[0], B[1]);
  nand nand_9 (M[0], nand_1_out, nand_1_out);
  nand nand_10 (M[1], nand_2_out, nand_3_out, nand_4_out, nand_5_out);
  nand nand_11 (M[2], nand_4_out, nand_6_out, nand_7_out);
  nand nand_12 (M[3], nand_7_out, nand_8_out);
endmodule

module MUX2 (
  input  A,
  input  S,
  input  B,
  output F
);

  wire and_1_out, and_2_out;

  and and_1 (and_1_out, A, ~S);  // AND_Gate
  and and_2 (and_2_out, S, B);
  or or_1 (F, and_1_out, and_2_out);
endmodule

module MUX4 (
  input  A,
  input  B,
  input  S0,
  input  S1,
  input  C,
  input  D,
  output F
);

  wire mux2_1_f, mux2_2_f;

  MUX2 mux2_1 (.A(A), .S(S0), .B(B), .F(mux2_1_f));
  MUX2 mux2_2 (.A(C), .S(S0), .B(D), .F(mux2_2_f));
  MUX2 mux2_3 (.A(mux2_1_f), .S(S1), .B(mux2_2_f), .F(F));
endmodule

module DEMUX2 (
  input  E,
  input  S,
  output A,
  output B
);

  and and_1 (A, E, ~S);  // AND_Gate
  and and_2 (B, S, E);
endmodule

module DEMUX4 (
  input  E,
  input  S0,
  input  S1,
  output A,
  output B,
  output C,
  output D
);

  wire demux2_1_a, demux2_1_b;

  DEMUX2 demux2_1 (.E(E), .S(S0), .A(demux2_1_a), .B(demux2_1_b));
  DEMUX2 demux2_2 (.E(demux2_1_a), .S(S1), .A(A), .B(B));
  DEMUX2 demux2_3 (.E(demux2_1_b), .S(S1), .A(C), .B(D));
endmodule

module Igual (
  input  [3:0] A,
  input  [3:0] B,
  output F
);

  wire xor_1_out, xor_2_out, xor_3_out, xor_4_out;

  xor xor_1 (xor_1_out, A[0], B[0]);
  xor xor_2 (xor_2_out, A[1], B[1]);
  xor xor_3 (xor_3_out, A[2], B[2]);
  xor xor_4 (xor_4_out, A[3], B[3]);
  nor nor_1 (F, xor_1_out, xor_2_out, xor_3_out, xor_4_out);
endmodule
