// Logisim project TPu4.circ as structural Verilog
module FFRSAsync (
  input  R,
  input  S,
  output Q,
  output NotQ
);

  nor nor_1 (Q, R, NotQ);
  nor nor_2 (NotQ, Q, S);
endmodule

module FFRSSync (
  input  R,
  input  E,
  input  S,
  output Q,
  output NotQ
);

  wire and_1_out, and_2_out;

  and and_1 (and_1_out, R, E);
  and and_2 (and_2_out, E, S);
  nor nor_1 (Q, and_1_out, NotQ);
  nor nor_2 (NotQ, Q, and_2_out);
endmodule

module FFDSyncPLevel (
  input  D,
  input  E,
  output Q,
  output NotQ
);

  wire and_1_out, and_2_out;

  and and_1 (and_1_out, ~D, E);  // AND_Gate
  and and_2 (and_2_out, E, D);
  nor nor_1 (Q, and_1_out, NotQ);
  nor nor_2 (NotQ, Q, and_2_out);
endmodule

module DetectorFlancoAsc (
  input  Clock,
  output F
);

  wire not_1_out, not_2_out, not_3_out;

  not not_1 (not_1_out, not_2_out);
  not not_2 (not_2_out, Clock);
  not not_3 (not_3_out, not_1_out);
  and and_1 (F, Clock, not_3_out);
endmodule

module FFDSyncFAscendente (
  input  R,
  input  D,
  input  Clock,
  input  S,
  output Q,
  output NotQ
);

  wire and_1_out, and_2_out, detectorflancoasc_1_f, or_1_out, or_2_out;

  DetectorFlancoAsc detectorflancoasc_1 (.Clock(Clock), .F(detectorflancoasc_1_f));
  and and_1 (and_1_out, ~D, detectorflancoasc_1_f);  // AND_Gate
  and and_2 (and_2_out, detectorflancoasc_1_f, D);
  or or_1 (or_1_out, R, and_1_out);
  or or_2 (or_2_out, and_2_out, S);
  nor nor_1 (Q, or_1_out, NotQ);
  nor nor_2 (NotQ, Q, or_2_out);
endmodule

module OneHotCounter (
  input  Clock,
  input  S
);

  wire ffdsyncfascendente_1_q, ffdsyncfascendente_2_q, ffdsyncfascendente_3_q, ffdsyncfascendente_4_q;

  LED led_1 (.in(ffdsyncfascendente_1_q));
  FFDSyncFAscendente ffdsyncfascendente_1 (
    .D(ffdsyncfascendente_4_q), .Clock(Clock), .S(S), .Q(ffdsyncfascendente_1_q));  // open: R, NotQ
  LED led_2 (.in(ffdsyncfascendente_2_q));
  FFDSyncFAscendente ffdsyncfascendente_2 (
    .D(ffdsyncfascendente_1_q), .Clock(Clock), .Q(ffdsyncfascendente_2_q));  // open: R, S, NotQ
  LED led_3 (.in(ffdsyncfascendente_3_q));
  FFDSyncFAscendente ffdsyncfascendente_3 (
    .D(ffdsyncfascendente_2_q), .Clock(Clock), .Q(ffdsyncfascendente_3_q));  // open: R, S, NotQ
  LED led_4 (.in(ffdsyncfascendente_4_q));
  FFDSyncFAscendente ffdsyncfascendente_4 (
    .D(ffdsyncfascendente_3_q), .Clock(Clock), .Q(ffdsyncfascendente_4_q));  // open: R, S, NotQ
endmodule

module FFTSyncFAscendente (
  input  R,
  input  T,
  input  Clock,
  input  S,
  output Q,
  output NotQ
);

  wire xor_1_out;

  xor xor_1 (xor_1_out, Q, T);
  FFDSyncFAscendente ffdsyncfascendente_1 (.D(xor_1_out), .Clock(Clock), .R(R), .S(S), .Q(Q), .NotQ(NotQ));
endmodule

module LatchReg8Bit (
  input  [7:0] Din,
  input  Clock,
  input  R,
  output [7:0] Dout
);

  FFDSyncFAscendente ffdsyncfascendente_1 (.D(Din[7]), .Clock(Clock), .R(R), .Q(Dout[7]));  // open: S, NotQ
  FFDSyncFAscendente ffdsyncfascendente_2 (.D(Din[6]), .Clock(Clock), .R(R), .Q(Dout[6]));  // open: S, NotQ
  FFDSyncFAscendente ffdsyncfascendente_3 (.D(Din[5]), .Clock(Clock), .R(R), .Q(Dout[5]));  // open: S, NotQ
  FFDSyncFAscendente ffdsyncfascendente_4 (.D(Din[3]), .Clock(Clock), .R(R), .Q(Dout[3]));  // open: S, NotQ
  FFDSyncFAscendente ffdsyncfascendente_5 (.D(Din[4]), .Clock(Clock), .R(R), .Q(Dout[4]));  // open: S, NotQ
  FFDSyncFAscendente ffdsyncfascendente_6 (.D(Din[2]), .Clock(Clock), .R(R), .Q(Dout[2]));  // open: S, NotQ
  FFDSyncFAscendente ffdsyncfascendente_7 (.D(Din[1]), .Clock(Clock), .R(R), .Q(Dout[1]));  // open: S, NotQ
  FFDSyncFAscendente ffdsyncfascendente_8 (.D(Din[0]), .Clock(Clock), .R(R), .Q(Dout[0]));  // open: S, NotQ
endmodule

module Sumador8Bits (
  input  Cin,
  input  [7:0] A,
  input  [7:0] B,
  output [7:0] S,
  output Cout
);

  wire fulladder_1_cout, fulladder_2_cout, fulladder_3_cout, fulladder_4_cout, fulladder_5_cout,
       fulladder_6_cout, fulladder_7_cout;

  FullAdder fulladder_1 (.A(A[0]), .B(B[0]), .Cin(Cin), .S(S[0]), .Cout(fulladder_1_cout));
  FullAdder fulladder_2 (.A(fulladder_1_cout), .B(A[1]), .Cin(B[1]), .S(S[1]), .Cout(fulladder_2_cout));
  FullAdder fulladder_3 (.A(fulladder_2_cout), .B(A[2]), .Cin(B[2]), .S(S[2]), .Cout(fulladder_3_cout));
  FullAdder fulladder_4 (.A(fulladder_3_cout), .B(A[3]), .Cin(B[3]), .S(S[3]), .Cout(fulladder_4_cout));
  FullAdder fulladder_5 (.A(fulladder_4_cout), .B(A[4]), .Cin(B[4]), .S(S[4]), .Cout(fulladder_5_cout));
  FullAdder fulladder_6 (.A(fulladder_5_cout), .B(A[5]), .Cin(B[5]), .S(S[5]), .Cout(fulladder_6_cout));
  FullAdder fulladder_7 (.A(fulladder_6_cout), .B(A[6]), .Cin(B[6]), .S(S[6]), .Cout(fulladder_7_cout));
  FullAdder fulladder_8 (.A(fulladder_7_cout), .B(A[7]), .Cin(B[7]), .S(S[7]), .Cout(Cout));
endmodule

module FullAdder (
  input  A,
  input  B,
  input  Cin,
  output S,
  output Cout
);

  wire and_1_out, and_2_out, and_3_out, xor_1_out;

  and and_1 (and_1_out, A, B);
  and and_2 (and_2_out, A, Cin);
  and and_3 (and_3_out, B, Cin);
  xor xor_1 (xor_1_out, A, B);
  xor xor_2 (S, xor_1_out, Cin);
  or or_1 (Cout, and_1_out, and_2_out, and_3_out);
endmodule

module E02 (
  input  [7:0] A,
  input  Clock,
  input  Clock_2,
  input  [7:0] B,
  input  Clock_3
);

  wire [7:0] latchreg8bit_1_dout, latchreg8bit_2_dout, latchreg8bit_3_dout, sumador8bits_1_s;

  Hex_Digit_Display hex_digit_display_1 (.value(A[3:0]));  // open: dp
  Hex_Digit_Display hex_digit_display_2 (.value(A[7:4]));  // open: dp
  Hex_Digit_Display hex_digit_display_3 (.value(B[7:4]));  // open: dp
  Hex_Digit_Display hex_digit_display_4 (.value(B[3:0]));  // open: dp
  LatchReg8Bit latchreg8bit_1 (.Din(A), .Clock(Clock_2), .Dout(latchreg8bit_1_dout));  // open: R
  LatchReg8Bit latchreg8bit_2 (.Din(B), .Clock(Clock_3), .Dout(latchreg8bit_2_dout));  // open: R
  Hex_Digit_Display hex_digit_display_5 (.value(latchreg8bit_1_dout[7:4]));  // open: dp
  Hex_Digit_Display hex_digit_display_6 (.value(latchreg8bit_2_dout[7:4]));  // open: dp
  Hex_Digit_Display hex_digit_display_7 (.value(latchreg8bit_1_dout[3:0]));  // open: dp
  Hex_Digit_Display hex_digit_display_8 (.value(latchreg8bit_2_dout[3:0]));  // open: dp
  Sumador8Bits sumador8bits_1 (
    .A(latchreg8bit_1_dout), .B(latchreg8bit_2_dout), .S(sumador8bits_1_s));  // open: Cin, Cout
  Hex_Digit_Display hex_digit_display_9 (.value(sumador8bits_1_s[7:4]));  // open: dp
  Hex_Digit_Display hex_digit_display_10 (.value(sumador8bits_1_s[3:0]));  // open: dp
  LatchReg8Bit latchreg8bit_3 (.Din(sumador8bits_1_s), .Clock(Clock), .Dout(latchreg8bit_3_dout));  // open: R
  Hex_Digit_Display hex_digit_display_11 (.value(latchreg8bit_3_dout[7:4]));  // open: dp
  Hex_Digit_Display hex_digit_display_12 (.value(latchreg8bit_3_dout[3:0]));  // open: dp
endmodule

module E04 (
  input  [7:0] A,
  input  ClockA,
  input  ClockSum,
  input  RA,
  input  RSum,
  output [7:0] Sum
);

  wire [7:0] latchreg8bit2_1_dout, sumador8bits_1_s;

  Hex_Digit_Display hex_digit_display_1 (.value(A[7:4]));  // open: dp
  Hex_Digit_Display hex_digit_display_2 (.value(A[3:0]));  // open: dp
  LatchReg8Bit2 latchreg8bit2_1 (.Din(A), .Clock(ClockA), .R(RA), .Dout(latchreg8bit2_1_dout));
  Hex_Digit_Display hex_digit_display_3 (.value(latchreg8bit2_1_dout[3:0]));  // open: dp
  Hex_Digit_Display hex_digit_display_4 (.value(latchreg8bit2_1_dout[7:4]));  // open: dp
  Sumador8Bits sumador8bits_1 (.A(latchreg8bit2_1_dout), .B(Sum), .S(sumador8bits_1_s));  // open: Cin, Cout
  Hex_Digit_Display hex_digit_display_5 (.value(sumador8bits_1_s[3:0]));  // open: dp
  Hex_Digit_Display hex_digit_display_6 (.value(sumador8bits_1_s[7:4]));  // open: dp
  LatchReg8Bit2 latchreg8bit2_2 (.Din(sumador8bits_1_s), .Clock(ClockSum), .R(RSum), .Dout(Sum));
  Hex_Digit_Display hex_digit_display_7 (.value(Sum[7:4]));  // open: dp
  Hex_Digit_Display hex_digit_display_8 (.value(Sum[3:0]));  // open: dp
endmodule

module E05 (
  input  [7:0] in_1,
  input  Clock,
  input  R
);

  wire [7:0] latchreg8bit_1_dout, sumador8bits_1_s;

  Sumador8Bits sumador8bits_1 (.A(in_1), .B(latchreg8bit_1_dout), .S(sumador8bits_1_s));  // open: Cin, Cout
  Hex_Digit_Display hex_digit_display_1 (.value(sumador8bits_1_s[7:4]));  // open: dp
  Hex_Digit_Display hex_digit_display_2 (.value(sumador8bits_1_s[3:0]));  // open: dp
  LatchReg8Bit latchreg8bit_1 (.Din(sumador8bits_1_s), .Clock(Clock), .R(R), .Dout(latchreg8bit_1_dout));
  Hex_Digit_Display hex_digit_display_3 (.value(latchreg8bit_1_dout[7:4]));  // open: dp
  Hex_Digit_Display hex_digit_display_4 (.value(latchreg8bit_1_dout[3:0]));  // open: dp
endmodule

module E06 (
  input  [7:0] Variable,
  input  Seleccion,
  input  [7:0] Fijo,
  input  Clock,
  input  R,
  output [7:0] Sum
);

  wire [7:0] multiplexer_1_out, sumador8bits_1_s;

  Sumador8Bits sumador8bits_1 (.A(Fijo), .B(Sum), .S(sumador8bits_1_s));  // open: Cin, Cout
  Hex_Digit_Display hex_digit_display_1 (.value(sumador8bits_1_s[7:4]));  // open: dp
  Hex_Digit_Display hex_digit_display_2 (.value(sumador8bits_1_s[3:0]));  // open: dp
  Multiplexer #(.width(8), .enable("false")) multiplexer_1 (
    .in0(Variable), .in1(sumador8bits_1_s), .out(multiplexer_1_out), .sel(Seleccion));
  LatchReg8Bit2 latchreg8bit2_1 (.Din(multiplexer_1_out), .Clock(Clock), .R(R), .Dout(Sum));
  Hex_Digit_Display hex_digit_display_3 (.value(Sum[7:4]));  // open: dp
  Hex_Digit_Display hex_digit_display_4 (.value(Sum[3:0]));  // open: dp
endmodule

module E07 (
  input  [7:0] A,
  input  Clock,
  input  R,
  input  [7:0] B,
  output [7:0] Aux,
  output [7:0] Sum
);

  wire and_1_out, and_2_out, and_3_out, C1, F, not_1_out, Z;

  and and_1 (and_1_out, ~F, Clock);  // AND_Gate
  and and_2 (and_2_out, ~F, Clock);  // AND_Gate
  E06 e06_1 (.Variable(B), .Fijo({8{1'b1}}), .Clock(and_1_out), .R(R), .Seleccion(C1), .Sum(Sum));
  E04 e04_1 (.A(A), .ClockA(and_2_out), .ClockSum(and_2_out), .RA(R), .RSum(R), .Sum(Aux));
  nor nor_1 (Z, Sum[7], Sum[6], Sum[5], Sum[4], Sum[3], Sum[2], Sum[1], Sum[0]);
  and and_3 (and_3_out, C1, Z);
  not not_1 (not_1_out, Clock);
  D_Flip_Flop d_ff_1 (.D(Clock), .clk(Clock), .Q(C1), .reset(R));  // open: Qn, preset
  D_Flip_Flop d_ff_2 (.D(and_3_out), .clk(not_1_out), .Q(F), .reset(R));  // open: Qn, preset
endmodule

module LatchReg8Bit2 (
  input  [7:0] Din,
  input  Clock,
  input  R,
  output [7:0] Dout
);

  D_Flip_Flop d_ff_1 (.D(Din[7]), .clk(Clock), .Q(Dout[7]), .reset(R));  // open: Qn, preset
  D_Flip_Flop d_ff_2 (.D(Din[6]), .clk(Clock), .Q(Dout[6]), .reset(R));  // open: Qn, preset
  D_Flip_Flop d_ff_3 (.D(Din[5]), .clk(Clock), .Q(Dout[5]), .reset(R));  // open: Qn, preset
  D_Flip_Flop d_ff_4 (.D(Din[4]), .clk(Clock), .Q(Dout[4]), .reset(R));  // open: Qn, preset
  D_Flip_Flop d_ff_5 (.D(Din[3]), .clk(Clock), .Q(Dout[3]), .reset(R));  // open: Qn, preset
  D_Flip_Flop d_ff_6 (.D(Din[2]), .clk(Clock), .Q(Dout[2]), .reset(R));  // open: Qn, preset
  D_Flip_Flop d_ff_7 (.D(Din[1]), .clk(Clock), .Q(Dout[1]), .reset(R));  // open: Qn, preset
  D_Flip_Flop d_ff_8 (.D(Din[0]), .clk(Clock), .Q(Dout[0]), .reset(R));  // open: Qn, preset
endmodule

module SerieParalelo (
  input  Serie,
  input  Clock,
  output [7:0] Paralelo
);

  D_Flip_Flop d_ff_1 (.D(Serie), .clk(Clock), .Q(Paralelo[7]));  // open: Qn, preset, reset
  D_Flip_Flop d_ff_2 (.D(Paralelo[7]), .clk(Clock), .Q(Paralelo[6]));  // open: Qn, preset, reset
  D_Flip_Flop d_ff_3 (.D(Paralelo[6]), .clk(Clock), .Q(Paralelo[5]));  // open: Qn, preset, reset
  D_Flip_Flop d_ff_4 (.D(Paralelo[5]), .clk(Clock), .Q(Paralelo[4]));  // open: Qn, preset, reset
  D_Flip_Flop d_ff_5 (.D(Paralelo[4]), .clk(Clock), .Q(Paralelo[3]));  // open: Qn, preset, reset
  D_Flip_Flop d_ff_6 (.D(Paralelo[3]), .clk(Clock), .Q(Paralelo[2]));  // open: Qn, preset, reset
  D_Flip_Flop d_ff_7 (.D(Paralelo[2]), .clk(Clock), .Q(Paralelo[1]));  // open: Qn, preset, reset
  D_Flip_Flop d_ff_8 (.D(Paralelo[1]), .clk(Clock), .Q(Paralelo[0]));  // open: Qn, preset, reset
endmodule

module ParaleloSerie (
  input  [7:0] Paralelo,
  input  Latch,
  input  Clock,
  output Serie
);

  wire and_1_out, d_ff_1_q, d_ff_2_q, d_ff_3_q, d_ff_4_q, d_ff_5_q, d_ff_6_q, d_ff_7_q, d_ff_8_q;
  wire [2:0] contadorsyncascendentemod8_1_count;

  D_Flip_Flop d_ff_1 (.D(Paralelo[7]), .clk(Latch), .Q(d_ff_1_q));  // open: Qn, preset, reset
  D_Flip_Flop d_ff_2 (.D(Paralelo[6]), .clk(Latch), .Q(d_ff_2_q));  // open: Qn, preset, reset
  and and_1 (and_1_out, ~Latch, Clock);  // AND_Gate
  D_Flip_Flop d_ff_3 (.D(Paralelo[5]), .clk(Latch), .Q(d_ff_3_q));  // open: Qn, preset, reset
  ContadorSyncAscendenteMod8 contadorsyncascendentemod8_1 (
    .Clock(and_1_out), .R(Latch), .Count(contadorsyncascendentemod8_1_count));
  D_Flip_Flop d_ff_4 (.D(Paralelo[4]), .clk(Latch), .Q(d_ff_4_q));  // open: Qn, preset, reset
  D_Flip_Flop d_ff_5 (.D(Paralelo[3]), .clk(Latch), .Q(d_ff_5_q));  // open: Qn, preset, reset
  Multiplexer #(.select(3), .enable("false")) multiplexer_1 (
    .in0(d_ff_8_q), .in1(d_ff_7_q), .in2(d_ff_6_q), .in3(d_ff_5_q), .in4(d_ff_4_q), .in5(d_ff_3_q),
    .in6(d_ff_2_q), .in7(d_ff_1_q), .out(Serie), .sel(contadorsyncascendentemod8_1_count));
  D_Flip_Flop d_ff_6 (.D(Paralelo[2]), .clk(Latch), .Q(d_ff_6_q));  // open: Qn, preset, reset
  D_Flip_Flop d_ff_7 (.D(Paralelo[1]), .clk(Latch), .Q(d_ff_7_q));  // open: Qn, preset, reset
  D_Flip_Flop d_ff_8 (.D(Paralelo[0]), .clk(Latch), .Q(d_ff_8_q));  // open: Qn, preset, reset
endmodule

module ContadorSyncAscendenteMod8 (
  input  Clock,
  input  R,
  output [2:0] Count
);

  wire and_1_out;

  T_Flip_Flop t_ff_1 (.T(1'b1), .clk(Clock), .Q(Count[0]), .reset(R));  // open: Qn, preset
  T_Flip_Flop t_ff_2 (.T(Count[0]), .clk(Clock), .Q(Count[1]), .reset(R));  // open: Qn, preset
  and and_1 (and_1_out, Count[0], Count[1]);
  T_Flip_Flop t_ff_3 (.T(and_1_out), .clk(Clock), .Q(Count[2]), .reset(R));  // open: Qn, preset
endmodule

module E08 (
  input  [7:0] Paralelo,
  input  Latch,
  input  Clock,
  output [7:0] Paralelo_2
);

  wire paraleloserie_1_serie;

  ParaleloSerie paraleloserie_1 (.Paralelo(Paralelo), .Latch(Latch), .Clock(Clock), .Serie(paraleloserie_1_serie));
  SerieParalelo serieparalelo_1 (.Serie(paraleloserie_1_serie), .Clock(Clock), .Paralelo(Paralelo_2));
endmodule

module E09 (
  input  Clock,
  output [3:0] Count
);

  T_Flip_Flop t_ff_1 (.T(1'b1), .clk(Clock), .Q(Count[0]));  // open: Qn, reset, preset
  T_Flip_Flop t_ff_2 (.T(1'b1), .clk(Count[0]), .Q(Count[1]));  // open: Qn, reset, preset
  T_Flip_Flop t_ff_3 (.T(1'b1), .clk(Count[1]), .Q(Count[2]));  // open: Qn, reset, preset
  T_Flip_Flop t_ff_4 (.T(1'b1), .clk(Count[2]), .Q(Count[3]));  // open: Qn, reset, preset
endmodule

module E10 (
  input  Clock,
  input  R,
  output [3:0] Count
);

  wire and_1_out, and_2_out;

  T_Flip_Flop t_ff_1 (.T(1'b1), .clk(Clock), .Q(Count[0]), .reset(R));  // open: Qn, preset
  T_Flip_Flop t_ff_2 (.T(Count[0]), .clk(Clock), .Q(Count[1]), .reset(R));  // open: Qn, preset
  and and_1 (and_1_out, Count[0], Count[1]);
  T_Flip_Flop t_ff_3 (.T(and_1_out), .clk(Clock), .Q(Count[2]), .reset(R));  // open: Qn, preset
  and and_2 (and_2_out, Count[0], Count[1], Count[2]);
  T_Flip_Flop t_ff_4 (.T(and_2_out), .clk(Clock), .Q(Count[3]));  // open: Qn, reset, preset
endmodule
