// Logisim project TPu4v2.circ as structural Verilog
module FFRSAsync (
  input  R,
  input  S,
  output Q,
  output NotQ
);

  nor nor_1 (Q, R, NotQ);
  nor nor_2 (NotQ, Q, S);
endmodule

module FFRSSync (
  input  R,
  input  E,
  input  S,
  output Q,
  output NotQ
);

  wire and_1_out, and_2_out;

  and and_1 (and_1_out, R, E);
  and and_2 (and_2_out, E, S);
  nor nor_1 (Q, and_1_out, NotQ);
  nor nor_2 (NotQ, Q, and_2_out);
endmodule

module FFDSyncPLevel (
  input  D,
  input  E,
  output Q,
  output NotQ
);

  wire and_1_out, and_2_out;

  and and_1 (and_1_out, ~D, E);  // AND_Gate
  and and_2 (and_2_out, E, D);
  nor nor_1 (Q, and_1_out, NotQ);
  nor nor_2 (NotQ, Q, and_2_out);
endmodule

module DetectorFlancoAsc (
  input  Clock,
  output F
);

  wire not_1_out, not_2_out, not_3_out;

  not not_1 (not_1_out, Clock);
  not not_2 (not_2_out, not_1_out);
  not not_3 (not_3_out, not_2_out);
  and and_1 (F, Clock, not_3_out);
endmodule

module FFDSyncAscendente (
  input  R,
  input  D,
  input  Clock,
  input  S,
  output Q,
  output NotQ
);

  wire and_1_out, and_2_out, detectorflancoasc_1_f, or_1_out, or_2_out;

  DetectorFlancoAsc detectorflancoasc_1 (.Clock(Clock), .F(detectorflancoasc_1_f));
  and and_1 (and_1_out, ~D, detectorflancoasc_1_f);  // AND_Gate
  and and_2 (and_2_out, detectorflancoasc_1_f, D);
  or or_1 (or_1_out, R, and_1_out);
  or or_2 (or_2_out, and_2_out, S);
  nor nor_1 (Q, or_1_out, NotQ);
  nor nor_2 (NotQ, Q, or_2_out);
endmodule

module OneHotCounter (
  input  Clock,
  input  S
);

  wire d_ff_1_q, d_ff_2_q, d_ff_3_q, d_ff_4_q;

  LED led_1 (.in(d_ff_1_q));
  D_Flip_Flop d_ff_1 (.D(d_ff_4_q), .clk(Clock), .Q(d_ff_1_q), .preset(S));  // open: Qn, reset
  D_Flip_Flop d_ff_2 (.D(d_ff_1_q), .clk(Clock), .Q(d_ff_2_q));  // open: Qn, preset, reset
  LED led_2 (.in(d_ff_2_q));
  D_Flip_Flop d_ff_3 (.D(d_ff_2_q), .clk(Clock), .Q(d_ff_3_q));  // open: Qn, preset, reset
  LED led_3 (.in(d_ff_3_q));
  D_Flip_Flop d_ff_4 (.D(d_ff_3_q), .clk(Clock), .Q(d_ff_4_q));  // open: Qn, preset, reset
  LED led_4 (.in(d_ff_4_q));
endmodule

module LatchReg8Bit (
  input  [7:0] Din,
  input  Clock,
  input  R,
  output [7:0] Dout
);

  D_Flip_Flop d_ff_1 (.D(Din[7]), .clk(Clock), .Q(Dout[7]), .reset(R));  // open: Qn, preset
  D_Flip_Flop d_ff_2 (.D(Din[6]), .clk(Clock), .Q(Dout[6]), .reset(R));  // open: Qn, preset
  D_Flip_Flop d_ff_3 (.D(Din[5]), .clk(Clock), .Q(Dout[5]), .reset(R));  // open: Qn, preset
  D_Flip_Flop d_ff_4 (.D(Din[4]), .clk(Clock), .Q(Dout[4]), .reset(R));  // open: Qn, preset
  D_Flip_Flop d_ff_5 (.D(Din[3]), .clk(Clock), .Q(Dout[3]), .reset(R));  // open: Qn, preset
  D_Flip_Flop d_ff_6 (.D(Din[2]), .clk(Clock), .Q(Dout[2]), .reset(R));  // open: Qn, preset
  D_Flip_Flop d_ff_7 (.D(Din[1]), .clk(Clock), .Q(Dout[1]), .reset(R));  // open: Qn, preset
  D_Flip_Flop d_ff_8 (.D(Din[0]), .clk(Clock), .Q(Dout[0]), .reset(R));  // open: Qn, preset
endmodule

module FullAdder (
  input  A,
  input  B,
  input  Cin,
  output S,
  output Cout
);

  wire and_1_out, and_2_out, and_3_out, xor_1_out;

  xor xor_1 (xor_1_out, A, B);
  and and_1 (and_1_out, A, B);
  and and_2 (and_2_out, A, Cin);
  and and_3 (and_3_out, B, Cin);
  xor xor_2 (S, xor_1_out, Cin);
  or or_1 (Cout, and_1_out, and_2_out, and_3_out);
endmodule

module Sumador8Bits (
  input  Cin,
  input  [7:0] A,
  input  [7:0] B,
  output [7:0] S,
  output Cout
);

  wire fulladder_1_cout, fulladder_2_cout, fulladder_3_cout, fulladder_4_cout, fulladder_5_cout,
       fulladder_6_cout, fulladder_7_cout;

  FullAdder fulladder_1 (.A(A[0]), .B(B[0]), .Cin(Cin), .S(S[0]), .Cout(fulladder_1_cout));
  FullAdder fulladder_2 (.A(fulladder_1_cout), .B(A[1]), .Cin(B[1]), .S(S[1]), .Cout(fulladder_2_cout));
  FullAdder fulladder_3 (.A(fulladder_2_cout), .B(A[2]), .Cin(B[2]), .S(S[2]), .Cout(fulladder_3_cout));
  FullAdder fulladder_4 (.A(fulladder_3_cout), .B(A[3]), .Cin(B[3]), .S(S[3]), .Cout(fulladder_4_cout));
  FullAdder fulladder_5 (.A(fulladder_4_cout), .B(A[4]), .Cin(B[4]), .S(S[4]), .Cout(fulladder_5_cout));
  FullAdder fulladder_6 (.A(fulladder_5_cout), .B(A[5]), .Cin(B[5]), .S(S[5]), .Cout(fulladder_6_cout));
  FullAdder fulladder_7 (.A(fulladder_6_cout), .B(A[6]), .Cin(B[6]), .S(S[6]), .Cout(fulladder_7_cout));
  FullAdder fulladder_8 (.A(fulladder_7_cout), .B(A[7]), .Cin(B[7]), .S(S[7]), .Cout(Cout));
endmodule

module E02 (
  input  in_1,
  input  [7:0] A,
  input  in_3,
  input  [7:0] B,
  input  Clock
);

  wire [3:0] latchreg8bit_2_dout, latchreg8bit_2_dout_2;
  wire [7:0] latchreg8bit_1_dout, latchreg8bit_3_dout, sumador8bits_1_s;

  Hex_Digit_Display hex_digit_display_1 (.value(A[7:4]));  // open: dp
  Hex_Digit_Display hex_digit_display_2 (.value(B[7:4]));  // open: dp
  Hex_Digit_Display hex_digit_display_3 (.value(B[3:0]));  // open: dp
  Hex_Digit_Display hex_digit_display_4 (.value(A[3:0]));  // open: dp
  LatchReg8Bit latchreg8bit_1 (.Din(A), .Clock(in_3), .Dout(latchreg8bit_1_dout));  // open: R
  LatchReg8Bit latchreg8bit_2 (.Din(B), .Clock(Clock), .Dout({latchreg8bit_2_dout, latchreg8bit_2_dout_2}));  // open: R
  Hex_Digit_Display hex_digit_display_5 (.value(latchreg8bit_1_dout[7:4]));  // open: dp
  Hex_Digit_Display hex_digit_display_6 (.value(latchreg8bit_1_dout[3:0]));  // open: dp
  Hex_Digit_Display hex_digit_display_7 (.value(latchreg8bit_2_dout));  // open: dp
  Hex_Digit_Display hex_digit_display_8 (.value(latchreg8bit_2_dout_2));  // open: dp
  Sumador8Bits sumador8bits_1 (
    .A(latchreg8bit_1_dout), .B({latchreg8bit_2_dout, latchreg8bit_2_dout_2}), .S(sumador8bits_1_s));  // open: Cin, Cout
  Hex_Digit_Display hex_digit_display_9 (.value(sumador8bits_1_s[7:4]));  // open: dp
  Hex_Digit_Display hex_digit_display_10 (.value(sumador8bits_1_s[3:0]));  // open: dp
  LatchReg8Bit latchreg8bit_3 (.Din(sumador8bits_1_s), .Clock(in_1), .Dout(latchreg8bit_3_dout));  // open: R
  Hex_Digit_Display hex_digit_display_11 (.value(latchreg8bit_3_dout[7:4]));  // open: dp
  Hex_Digit_Display hex_digit_display_12 (.value(latchreg8bit_3_dout[3:0]));  // open: dp
endmodule

module E04 (
  input  ClockSum,
  input  [7:0] A,
  input  RSum,
  input  ClockA,
  input  RA,
  output [7:0] Sum
);

  wire [7:0] latchreg8bit_1_dout, sumador8bits_1_s;

  Hex_Digit_Display hex_digit_display_1 (.value(A[7:4]));  // open: dp
  Hex_Digit_Display hex_digit_display_2 (.value(A[3:0]));  // open: dp
  LatchReg8Bit latchreg8bit_1 (.Din(A), .Clock(ClockA), .R(RA), .Dout(latchreg8bit_1_dout));
  Hex_Digit_Display hex_digit_display_3 (.value(latchreg8bit_1_dout[7:4]));  // open: dp
  Hex_Digit_Display hex_digit_display_4 (.value(latchreg8bit_1_dout[3:0]));  // open: dp
  Sumador8Bits sumador8bits_1 (.A(latchreg8bit_1_dout), .B(Sum), .S(sumador8bits_1_s));  // open: Cin, Cout
  Hex_Digit_Display hex_digit_display_5 (.value(sumador8bits_1_s[7:4]));  // open: dp
  Hex_Digit_Display hex_digit_display_6 (.value(sumador8bits_1_s[3:0]));  // open: dp
  LatchReg8Bit latchreg8bit_2 (.Din(sumador8bits_1_s), .Clock(ClockSum), .R(RSum), .Dout(Sum));
  Hex_Digit_Display hex_digit_display_7 (.value(Sum[7:4]));  // open: dp
  Hex_Digit_Display hex_digit_display_8 (.value(Sum[3:0]));  // open: dp
endmodule

module E06 (
  input  [7:0] Variable,
  input  Seleccion,
  input  Clock,
  input  [7:0] Fijo,
  input  R,
  output [7:0] Sum
);

  wire [3:0] sumador8bits_1_s, sumador8bits_1_s_2;
  wire [7:0] multiplexer_1_out;

  Sumador8Bits sumador8bits_1 (.A(Fijo), .B(Sum), .S({sumador8bits_1_s, sumador8bits_1_s_2}));  // open: Cin, Cout
  Hex_Digit_Display hex_digit_display_1 (.value(sumador8bits_1_s));  // open: dp
  Hex_Digit_Display hex_digit_display_2 (.value(sumador8bits_1_s_2));  // open: dp
  Multiplexer #(.width(8)) multiplexer_1 (
    .in0(Variable), .in1({sumador8bits_1_s, sumador8bits_1_s_2}), .out(multiplexer_1_out), .sel(Seleccion));
  LatchReg8Bit latchreg8bit_1 (.Din(multiplexer_1_out), .Clock(Clock), .R(R), .Dout(Sum));
  Hex_Digit_Display hex_digit_display_3 (.value(Sum[7:4]));  // open: dp
  Hex_Digit_Display hex_digit_display_4 (.value(Sum[3:0]));  // open: dp
endmodule

module E07 (
  input  [7:0] A,
  input  Clock,
  input  R,
  input  [7:0] B,
  output [7:0] Aux,
  output [7:0] Sum
);

  wire and_1_out, and_2_out, and_3_out, C1, F, not_1_out, Z;

  and and_1 (and_1_out, ~F, Clock);  // AND_Gate
  D_Flip_Flop d_ff_1 (.D(Clock), .clk(Clock), .Q(C1), .reset(R));  // open: Qn, preset
  and and_2 (and_2_out, C1, Z);
  D_Flip_Flop d_ff_2 (.D(and_2_out), .clk(not_1_out), .Q(F), .reset(R));  // open: Qn, preset
  not not_1 (not_1_out, Clock);
  and and_3 (and_3_out, ~F, Clock);  // AND_Gate
  E06 e06_1 (.Variable(B), .Seleccion(C1), .Clock(and_1_out), .Fijo({8{1'b1}}), .R(R), .Sum(Sum));
  E04 e04_1 (.ClockSum(and_3_out), .A(A), .RSum(R), .ClockA(and_3_out), .RA(R), .Sum(Aux));
  nor nor_1 (Z, Sum[7], Sum[6], Sum[5], Sum[4], Sum[3], Sum[2], Sum[1], Sum[0]);
endmodule

module SerieParalelo (
  input  Serie,
  input  Clock,
  output [7:0] Paralelo
);

  D_Flip_Flop d_ff_1 (.D(Serie), .clk(Clock), .Q(Paralelo[7]));  // open: Qn, preset, reset
  D_Flip_Flop d_ff_2 (.D(Paralelo[7]), .clk(Clock), .Q(Paralelo[6]));  // open: Qn, preset, reset
  D_Flip_Flop d_ff_3 (.D(Paralelo[6]), .clk(Clock), .Q(Paralelo[5]));  // open: Qn, preset, reset
  D_Flip_Flop d_ff_4 (.D(Paralelo[5]), .clk(Clock), .Q(Paralelo[4]));  // open: Qn, preset, reset
  D_Flip_Flop d_ff_5 (.D(Paralelo[4]), .clk(Clock), .Q(Paralelo[3]));  // open: Qn, preset, reset
  D_Flip_Flop d_ff_6 (.D(Paralelo[3]), .clk(Clock), .Q(Paralelo[2]));  // open: Qn, preset, reset
  D_Flip_Flop d_ff_7 (.D(Paralelo[2]), .clk(Clock), .Q(Paralelo[1]));  // open: Qn, preset, reset
  D_Flip_Flop d_ff_8 (.D(Paralelo[1]), .clk(Clock), .Q(Paralelo[0]));  // open: Qn, preset, reset
endmodule

module ContadorSyncAscMod8 (
  input  Clock,
  input  R,
  output [2:0] Count
);

  wire and_1_out;

  T_Flip_Flop t_ff_1 (.T(1'b1), .clk(Clock), .Q(Count[0]), .reset(R));  // open: Qn, preset
  T_Flip_Flop t_ff_2 (.T(Count[0]), .clk(Clock), .Q(Count[1]), .reset(R));  // open: Qn, preset
  and and_1 (and_1_out, Count[0], Count[1]);
  T_Flip_Flop t_ff_3 (.T(and_1_out), .clk(Clock), .Q(Count[2]), .reset(R));  // open: Qn, preset
endmodule

module ParaleloSerie (
  input  [7:0] Paralelo,
  input  Latch,
  input  Clock,
  output Serie
);

  wire and_1_out, d_ff_1_q, d_ff_2_q, d_ff_3_q, d_ff_4_q, d_ff_5_q, d_ff_6_q, d_ff_7_q, d_ff_8_q;
  wire [2:0] contadorsyncascmod8_1_count;

  D_Flip_Flop d_ff_1 (.D(Paralelo[7]), .clk(Latch), .Q(d_ff_1_q));  // open: Qn, preset, reset
  D_Flip_Flop d_ff_2 (.D(Paralelo[6]), .clk(Latch), .Q(d_ff_2_q));  // open: Qn, preset, reset
  and and_1 (and_1_out, ~Latch, Clock);  // AND_Gate
  D_Flip_Flop d_ff_3 (.D(Paralelo[5]), .clk(Latch), .Q(d_ff_3_q));  // open: Qn, preset, reset
  D_Flip_Flop d_ff_4 (.D(Paralelo[4]), .clk(Latch), .Q(d_ff_4_q));  // open: Qn, preset, reset
  ContadorSyncAscMod8 contadorsyncascmod8_1 (.Clock(and_1_out), .R(Latch), .Count(contadorsyncascmod8_1_count));
  Multiplexer #(.select(3)) multiplexer_1 (
    .in0(d_ff_8_q), .in1(d_ff_7_q), .in2(d_ff_6_q), .in3(d_ff_5_q), .in4(d_ff_4_q), .in5(d_ff_3_q),
    .in6(d_ff_2_q), .in7(d_ff_1_q), .out(Serie), .sel(contadorsyncascmod8_1_count));
  D_Flip_Flop d_ff_5 (.D(Paralelo[3]), .clk(Latch), .Q(d_ff_5_q));  // open: Qn, preset, reset
  D_Flip_Flop d_ff_6 (.D(Paralelo[2]), .clk(Latch), .Q(d_ff_6_q));  // open: Qn, preset, reset
  D_Flip_Flop d_ff_7 (.D(Paralelo[1]), .clk(Latch), .Q(d_ff_7_q));  // open: Qn, preset, reset
  D_Flip_Flop d_ff_8 (.D(Paralelo[0]), .clk(Latch), .Q(d_ff_8_q));  // open: Qn, preset, reset
endmodule

module E08 (
  input  [7:0] in_1,
  input  Latch,
  input  Clock,
  output [7:0] Paralelo
);

  wire paraleloserie_1_serie;

  ParaleloSerie paraleloserie_1 (.Paralelo(in_1), .Latch(Latch), .Clock(Clock), .Serie(paraleloserie_1_serie));
  SerieParalelo serieparalelo_1 (.Serie(paraleloserie_1_serie), .Clock(Clock), .Paralelo(Paralelo));
endmodule

module E09 (
  input  Clock,
  output [3:0] Count
);

  T_Flip_Flop t_ff_1 (.T(1'b1), .clk(Clock), .Q(Count[0]));  // open: Qn, reset, preset
  T_Flip_Flop t_ff_2 (.T(1'b1), .clk(Count[0]), .Q(Count[1]));  // open: Qn, reset, preset
  T_Flip_Flop t_ff_3 (.T(1'b1), .clk(Count[1]), .Q(Count[2]));  // open: Qn, reset, preset
  T_Flip_Flop t_ff_4 (.T(1'b1), .clk(Count[2]), .Q(Count[3]));  // open: Qn, reset, preset
endmodule

module E10 (
  input  Clock,
  input  R,
  output [3:0] Count
);

  wire and_1_out, and_2_out;

  T_Flip_Flop t_ff_1 (.T(1'b1), .clk(Clock), .Q(Count[0]), .reset(R));  // open: Qn, preset
  T_Flip_Flop t_ff_2 (.T(Count[0]), .clk(Clock), .Q(Count[1]), .reset(R));  // open: Qn, preset
  and and_1 (and_1_out, Count[0], Count[1]);
  T_Flip_Flop t_ff_3 (.T(and_1_out), .clk(Clock), .Q(Count[2]), .reset(R));  // open: Qn, preset
  and and_2 (and_2_out, Count[0], Count[1], Count[2]);
  T_Flip_Flop t_ff_4 (.T(and_2_out), .clk(Clock), .Q(Count[3]), .reset(R));  // open: Qn, preset
endmodule

module E11 (
  input  Tipo,
  input  Clock,
  output [4:0] F
);

  wire d_ff_5_qn, multiplexer_1_out, por_1_out;

  POR por_1 (.out(por_1_out));
  LED led_1 (.in(F[0]));
  D_Flip_Flop d_ff_1 (.D(multiplexer_1_out), .clk(Clock), .Q(F[0]), .preset(por_1_out));  // open: Qn, reset
  D_Flip_Flop d_ff_2 (.D(F[0]), .clk(Clock), .Q(F[1]));  // open: Qn, preset, reset
  LED led_2 (.in(F[1]));
  D_Flip_Flop d_ff_3 (.D(F[1]), .clk(Clock), .Q(F[2]));  // open: Qn, preset, reset
  LED led_3 (.in(F[2]));
  LED led_4 (.in(F[3]));
  D_Flip_Flop d_ff_4 (.D(F[2]), .clk(Clock), .Q(F[3]));  // open: Qn, preset, reset
  D_Flip_Flop d_ff_5 (.D(F[3]), .clk(Clock), .Q(F[4]), .Qn(d_ff_5_qn));  // open: preset, reset
  LED led_5 (.in(F[4]));
  Multiplexer multiplexer_1 (.in0(F[4]), .in1(d_ff_5_qn), .out(multiplexer_1_out), .sel(Tipo));
endmodule

module Contador6 (
  input  Clock,
  output [3:0] Count,
  output Carry
);

  wire and_2_out, and_3_out;

  T_Flip_Flop t_ff_1 (.T(1'b1), .clk(Clock), .Q(Count[0]), .reset(Carry));  // open: Qn, preset
  and and_1 (Carry, ~Count[3], Count[2], Count[1], ~Count[0]);  // AND_Gate
  T_Flip_Flop t_ff_2 (.T(Count[0]), .clk(Clock), .Q(Count[1]), .reset(Carry));  // open: Qn, preset
  and and_2 (and_2_out, Count[0], Count[1]);
  T_Flip_Flop t_ff_3 (.T(and_2_out), .clk(Clock), .Q(Count[2]), .reset(Carry));  // open: Qn, preset
  and and_3 (and_3_out, Count[0], Count[1], Count[2]);
  T_Flip_Flop t_ff_4 (.T(and_3_out), .clk(Clock), .Q(Count[3]), .reset(Carry));  // open: Qn, preset
endmodule

module Contador10 (
  input  Clock,
  input  R,
  output [3:0] Count,
  output Carry
);

  wire and_2_out, and_3_out, or_1_out;

  T_Flip_Flop t_ff_1 (.T(1'b1), .clk(Clock), .Q(Count[0]), .reset(or_1_out));  // open: Qn, preset
  or or_1 (or_1_out, R, Carry);
  T_Flip_Flop t_ff_2 (.T(Count[0]), .clk(Clock), .Q(Count[1]), .reset(or_1_out));  // open: Qn, preset
  and and_1 (Carry, Count[3], ~Count[2], Count[1], ~Count[0]);  // AND_Gate
  and and_2 (and_2_out, Count[0], Count[1]);
  T_Flip_Flop t_ff_3 (.T(and_2_out), .clk(Clock), .Q(Count[2]), .reset(or_1_out));  // open: Qn, preset
  and and_3 (and_3_out, Count[0], Count[1], Count[2]);
  T_Flip_Flop t_ff_4 (.T(and_3_out), .clk(Clock), .Q(Count[3]), .reset(or_1_out));  // open: Qn, preset
endmodule

module E13 (
);

  wire clock_1_out, contador10_1_carry;
  wire [3:0] contador6_1_count, contador10_1_count;

  Contador6 contador6_1 (.Clock(contador10_1_carry), .Count(contador6_1_count));  // open: Carry
  Clock clock_1 (.out(clock_1_out));
  Contador10 contador10_1 (.Clock(clock_1_out), .Count(contador10_1_count), .Carry(contador10_1_carry));  // open: R
  Hex_Digit_Display hex_digit_display_1 (.value(contador6_1_count));  // open: dp
  Hex_Digit_Display hex_digit_display_2 (.value(contador10_1_count));  // open: dp
endmodule

module E14 (
);

  wire and_1_out, and_2_out, and_3_out, clock_1_out, contador6_1_carry, contador6_2_carry,
       contador10_1_carry, contador10_2_carry, contador10_3_carry, or_1_out;
  wire [3:0] contador3_1_count, contador6_1_count, contador6_2_count, contador10_1_count, contador10_2_count,
       contador10_3_count;

  or or_1 (or_1_out, contador10_3_carry, and_3_out);
  Contador6 contador6_1 (.Clock(contador10_1_carry), .Count(contador6_1_count), .Carry(contador6_1_carry));
  Contador6 contador6_2 (.Clock(contador10_2_carry), .Count(contador6_2_count), .Carry(contador6_2_carry));
  Contador3 contador3_1 (.Clock(or_1_out), .Count(contador3_1_count));  // open: Carry
  Clock clock_1 (.out(clock_1_out));
  and and_1 (and_1_out, ~contador3_1_count[0], contador3_1_count[1], ~contador3_1_count[2], ~contador3_1_count[3]);  // AND_Gate
  Contador10 contador10_1 (.Clock(clock_1_out), .Count(contador10_1_count), .Carry(contador10_1_carry));  // open: R
  Contador10 contador10_2 (
    .Clock(contador6_1_carry), .Count(contador10_2_count), .Carry(contador10_2_carry));  // open: R
  Contador10 contador10_3 (
    .Clock(contador6_2_carry), .R(and_3_out), .Count(contador10_3_count), .Carry(contador10_3_carry));
  Hex_Digit_Display hex_digit_display_1 (.value(contador6_1_count));  // open: dp
  Hex_Digit_Display hex_digit_display_2 (.value(contador10_1_count));  // open: dp
  Hex_Digit_Display hex_digit_display_3 (.value(contador6_2_count));  // open: dp
  Hex_Digit_Display hex_digit_display_4 (.value(contador10_2_count));  // open: dp
  Hex_Digit_Display hex_digit_display_5 (.value(contador3_1_count));  // open: dp
  Hex_Digit_Display hex_digit_display_6 (.value(contador10_3_count));  // open: dp
  and and_2 (and_2_out, ~contador10_3_count[0], ~contador10_3_count[1], contador10_3_count[2], ~contador10_3_count[3]);  // AND_Gate
  and and_3 (and_3_out, and_2_out, and_1_out);
endmodule

module Contador3 (
  input  Clock,
  output [3:0] Count,
  output Carry
);

  wire and_2_out, and_3_out;

  T_Flip_Flop t_ff_1 (.T(1'b1), .clk(Clock), .Q(Count[0]), .reset(Carry));  // open: Qn, preset
  T_Flip_Flop t_ff_2 (.T(Count[0]), .clk(Clock), .Q(Count[1]), .reset(Carry));  // open: Qn, preset
  and and_1 (Carry, ~Count[3], ~Count[2], Count[1], Count[0]);  // AND_Gate
  and and_2 (and_2_out, Count[0], Count[1]);
  T_Flip_Flop t_ff_3 (.T(and_2_out), .clk(Clock), .Q(Count[2]), .reset(Carry));  // open: Qn, preset
  and and_3 (and_3_out, Count[0], Count[1], Count[2]);
  T_Flip_Flop t_ff_4 (.T(and_3_out), .clk(Clock), .Q(Count[3]), .reset(Carry));  // open: Qn, preset
endmodule

module Contador4 (
  input  Clock,
  output [3:0] Count,
  output Carry
);

  wire and_2_out, and_3_out;

  T_Flip_Flop t_ff_1 (.T(1'b1), .clk(Clock), .Q(Count[0]), .reset(Carry));  // open: Qn, preset
  T_Flip_Flop t_ff_2 (.T(Count[0]), .clk(Clock), .Q(Count[1]), .reset(Carry));  // open: Qn, preset
  and and_1 (Carry, ~Count[3], Count[2], ~Count[1], ~Count[0]);  // AND_Gate
  and and_2 (and_2_out, Count[0], Count[1]);
  T_Flip_Flop t_ff_3 (.T(and_2_out), .clk(Clock), .Q(Count[2]), .reset(Carry));  // open: Qn, preset
  and and_3 (and_3_out, Count[0], Count[1], Count[2]);
  T_Flip_Flop t_ff_4 (.T(and_3_out), .clk(Clock), .Q(Count[3]), .reset(Carry));  // open: Qn, preset
endmodule
