// Logisim project TPu5.circ as structural Verilog
module F01 (
  output [3:0] out_1
);

  wire and_1_out, and_2_out, and_3_out, and_4_out, and_5_out, and_6_out, and_7_out, Clock;
  wire [1:0] contadorsyncascmod8_1_count;

  Clock clock_1 (.out(Clock));
  ContadorSyncAscMod8 contadorsyncascmod8_1 (
    .Clock(Clock), .Count({out_1[3], contadorsyncascmod8_1_count}));  // open: R
  and and_1 (and_1_out, ~out_1[3], contadorsyncascmod8_1_count[1]);  // AND_Gate
  and and_2 (and_2_out, ~out_1[3], contadorsyncascmod8_1_count[0]);  // AND_Gate
  and and_3 (and_3_out, out_1[3], ~contadorsyncascmod8_1_count[1], ~contadorsyncascmod8_1_count[0]);  // AND_Gate
  and and_4 (and_4_out, ~out_1[3], contadorsyncascmod8_1_count[1]);  // AND_Gate
  and and_5 (and_5_out, out_1[3], ~contadorsyncascmod8_1_count[1]);  // AND_Gate
  and and_6 (and_6_out, out_1[3], ~contadorsyncascmod8_1_count[0]);  // AND_Gate
  and and_7 (and_7_out, ~out_1[3], contadorsyncascmod8_1_count[1], contadorsyncascmod8_1_count[0]);  // AND_Gate
  or or_1 (out_1[0], and_1_out, and_2_out, and_3_out);
  or or_2 (out_1[1], and_5_out, and_4_out);
  or or_3 (out_1[2], and_5_out, and_6_out, and_7_out);
  // Digital_Oscilloscope #(.nState(4)) digital_oscilloscope_1: pin names not known; wires that end beside it: Clock, out_1[0], out_1[1], out_1[2], out_1[3]

  // Other names for the same wires on the sheet: Johnson[3:0] = out_1
endmodule

module ContadorSyncAscMod8 (
  input  Clock,
  input  R,
  output [2:0] Count
);

  wire and_1_out;

  T_Flip_Flop t_ff_1 (.T(1'b1), .clk(Clock), .Q(Count[0]), .reset(R));  // open: Qn, preset
  T_Flip_Flop t_ff_2 (.T(Count[0]), .clk(Clock), .Q(Count[1]), .reset(R));  // open: Qn, preset
  and and_1 (and_1_out, Count[0], Count[1]);
  T_Flip_Flop t_ff_3 (.T(and_1_out), .clk(Clock), .Q(Count[2]), .reset(R));  // open: Qn, preset
endmodule

module JohnsonOneHot10Bits (
  input  Clock,
  input  Tipo,
  output [9:0] F
);

  wire d_ff_10_qn, multiplexer_1_out, por_1_out;

  D_Flip_Flop d_ff_1 (.D(multiplexer_1_out), .clk(Clock), .Q(F[0]), .preset(por_1_out));  // open: Qn, reset
  POR por_1 (.out(por_1_out));
  LED led_1 (.in(F[0]));
  D_Flip_Flop d_ff_2 (.D(F[0]), .clk(Clock), .Q(F[1]));  // open: Qn, preset, reset
  LED led_2 (.in(F[1]));
  D_Flip_Flop d_ff_3 (.D(F[1]), .clk(Clock), .Q(F[2]));  // open: Qn, preset, reset
  LED led_3 (.in(F[2]));
  D_Flip_Flop d_ff_4 (.D(F[2]), .clk(Clock), .Q(F[3]));  // open: Qn, preset, reset
  LED led_4 (.in(F[3]));
  D_Flip_Flop d_ff_5 (.D(F[3]), .clk(Clock), .Q(F[4]));  // open: Qn, preset, reset
  LED led_5 (.in(F[4]));
  D_Flip_Flop d_ff_6 (.D(F[4]), .clk(Clock), .Q(F[5]));  // open: Qn, preset, reset
  LED led_6 (.in(F[5]));
  D_Flip_Flop d_ff_7 (.D(F[5]), .clk(Clock), .Q(F[6]));  // open: Qn, preset, reset
  LED led_7 (.in(F[6]));
  D_Flip_Flop d_ff_8 (.D(F[6]), .clk(Clock), .Q(F[7]));  // open: Qn, preset, reset
  LED led_8 (.in(F[7]));
  D_Flip_Flop d_ff_9 (.D(F[7]), .clk(Clock), .Q(F[8]));  // open: Qn, preset, reset
  LED led_9 (.in(F[8]));
  D_Flip_Flop d_ff_10 (.D(F[8]), .clk(Clock), .Q(F[9]), .Qn(d_ff_10_qn));  // open: preset, reset
  LED led_10 (.in(F[9]));
  Multiplexer multiplexer_1 (.in0(d_ff_10_qn), .in1(F[9]), .out(multiplexer_1_out), .sel(Tipo));
endmodule

module F02 (
);

  wire clock_1_out;
  wire [3:0] or_1_out;
  wire [9:0] johnsononehot10bits_1_f;

  Clock clock_1 (.out(clock_1_out));
  JohnsonOneHot10Bits johnsononehot10bits_1 (.Clock(clock_1_out), .Tipo(1'b1), .F(johnsononehot10bits_1_f));
  or or_1 (or_1_out[0], johnsononehot10bits_1_f[1], johnsononehot10bits_1_f[3], johnsononehot10bits_1_f[5], johnsononehot10bits_1_f[7], johnsononehot10bits_1_f[9]);
  or or_2 (or_1_out[1], johnsononehot10bits_1_f[2], johnsononehot10bits_1_f[3], johnsononehot10bits_1_f[6], johnsononehot10bits_1_f[7]);
  or or_3 (or_1_out[2], johnsononehot10bits_1_f[4], johnsononehot10bits_1_f[5], johnsononehot10bits_1_f[6], johnsononehot10bits_1_f[7]);
  or or_4 (or_1_out[3], johnsononehot10bits_1_f[8], johnsononehot10bits_1_f[9]);
  Hex_Digit_Display hex_digit_display_1 (.value(or_1_out));  // open: dp
endmodule

module F03 (
  output [3:0] out_1
);

  wire clock_1_out;
  wire [4:0] johnsononehot5bits_1_f;

  Clock clock_1 (.out(clock_1_out));
  JohnsonOneHot5Bits johnsononehot5bits_1 (.Clock(clock_1_out), .F(johnsononehot5bits_1_f));  // open: Tipo
  Multiplexer #(.select(5), .width(4)) multiplexer_1 (
    .in0(4'b0000), .in1(4'b0001), .in3(4'b0010), .in7(4'b0011), .in15(4'b0100), .in16(4'b1111),
    .in24(4'b1110), .in28(4'b1101), .in30(4'b1100), .in31(4'b1011), .out(out_1), .sel(johnsononehot5bits_1_f));  // open: in2, in4, in5, in6, in8, in9, in10, in11, in12, in13, in14, in17, in18, in19, in20, in21, in22, in23, in25, in26, in27, in29
endmodule

module JohnsonOneHot5Bits (
  input  Clock,
  input  Tipo,
  output [4:0] F
);

  wire d_ff_5_qn, multiplexer_1_out, por_1_out;

  D_Flip_Flop d_ff_1 (.D(multiplexer_1_out), .clk(Clock), .Q(F[0]), .preset(por_1_out));  // open: Qn, reset
  POR por_1 (.out(por_1_out));
  LED led_1 (.in(F[0]));
  D_Flip_Flop d_ff_2 (.D(F[0]), .clk(Clock), .Q(F[1]));  // open: Qn, preset, reset
  LED led_2 (.in(F[1]));
  D_Flip_Flop d_ff_3 (.D(F[1]), .clk(Clock), .Q(F[2]));  // open: Qn, preset, reset
  LED led_3 (.in(F[2]));
  D_Flip_Flop d_ff_4 (.D(F[2]), .clk(Clock), .Q(F[3]));  // open: Qn, preset, reset
  LED led_4 (.in(F[3]));
  D_Flip_Flop d_ff_5 (.D(F[3]), .clk(Clock), .Q(F[4]), .Qn(d_ff_5_qn));  // open: preset, reset
  LED led_5 (.in(F[4]));
  Multiplexer multiplexer_1 (.in0(d_ff_5_qn), .in1(F[4]), .out(multiplexer_1_out), .sel(Tipo));
endmodule

module Johnson3Bits (
  input  Clock,
  output [2:0] F
);

  wire not_1_out, por_1_out;

  not not_1 (not_1_out, F[2]);
  POR por_1 (.out(por_1_out));
  D_Flip_Flop d_ff_1 (.D(not_1_out), .clk(Clock), .Q(F[0]), .preset(por_1_out));  // open: Qn, reset
  LED led_1 (.in(F[0]));
  D_Flip_Flop d_ff_2 (.D(F[0]), .clk(Clock), .Q(F[1]));  // open: Qn, preset, reset
  LED led_2 (.in(F[1]));
  D_Flip_Flop d_ff_3 (.D(F[1]), .clk(Clock), .Q(F[2]));  // open: Qn, preset, reset
  LED led_3 (.in(F[2]));
endmodule

module F04 (
);

  wire Clk, P;
  wire [2:0] johnson3bits_1_f;

  Clock clock_1 (.out(Clk));
  // Digital_Oscilloscope digital_oscilloscope_1: pin names not known; wires that end beside it: Clk, P
  Johnson3Bits johnson3bits_1 (.Clock(Clk), .F(johnson3bits_1_f));
  Multiplexer #(.select(3)) multiplexer_1 (
    .in0(1'b1), .in1(1'b1), .in3(1'b0), .in4(1'b0), .in6(1'b0), .in7(1'b0), .out(P), .sel(johnson3bits_1_f));  // open: in2, in5
endmodule

module F05 (
  input  A,
  input  R
);

  wire and_1_out, and_2_out, and_3_out, and_4_out, and_5_out, Clock, or_1_out, or_2_out, S0, S1;

  Clock clock_1 (.out(Clock));
  and and_1 (and_1_out, S1, ~S0);  // AND_Gate
  LED F (.in(and_1_out));
  and and_2 (and_2_out, ~S1, S0);  // AND_Gate
  and and_3 (and_3_out, S1, ~A);  // AND_Gate
  and and_4 (and_4_out, ~S0, A);  // AND_Gate
  and and_5 (and_5_out, ~S1, S0, ~A);  // AND_Gate
  or or_1 (or_1_out, and_2_out, and_3_out);
  or or_2 (or_2_out, and_4_out, and_5_out);
  D_Flip_Flop d_ff_1 (.D(or_1_out), .clk(Clock), .Q(S1), .reset(R));  // open: Qn, preset
  D_Flip_Flop d_ff_2 (.D(or_2_out), .clk(Clock), .Q(S0), .reset(R));  // open: Qn, preset
endmodule

module F07 (
  input  A1,
  input  A0,
  input  R
);

  wire and_1_out, and_2_out, and_3_out, Clock, or_1_out, or_2_out, or_3_out, or_4_out, or_5_out, S0, S1;

  Clock clock_1 (.out(Clock));
  and and_1 (and_1_out, S1, S0);
  LED G (.in(and_1_out));
  or or_1 (or_1_out, S1, S0, A1);
  or or_2 (or_2_out, S1, A1, A0);
  or or_3 (or_3_out, S1, S0, A0);
  or or_4 (or_4_out, S0, A1, A0);
  or or_5 (or_5_out, S1, ~S0, A1, ~A0);  // OR_Gate
  and and_2 (and_2_out, or_1_out, or_2_out);
  and and_3 (and_3_out, or_3_out, or_4_out, or_5_out);
  D_Flip_Flop d_ff_1 (.D(and_2_out), .clk(Clock), .Q(S1), .reset(R));  // open: Qn, preset
  D_Flip_Flop d_ff_2 (.D(and_3_out), .clk(Clock), .Q(S0), .reset(R));  // open: Qn, preset
endmodule

module F08 (
  output [2:0] F
);

  wire and_1_out, and_2_out, and_3_out, clock_1_out, not_1_out, or_1_out, xnor_1_out;

  Clock clock_1 (.out(clock_1_out));
  D_Flip_Flop C0 (.D(not_1_out), .clk(clock_1_out), .Q(F[0]));  // open: Qn, preset, reset
  not not_1 (not_1_out, F[0]);
  xnor xnor_1 (xnor_1_out, F[1], F[0]);
  D_Flip_Flop C1 (.D(xnor_1_out), .clk(clock_1_out), .Q(F[1]));  // open: Qn, preset, reset
  and and_1 (and_1_out, F[2], F[0]);
  and and_2 (and_2_out, F[2], F[1]);
  and and_3 (and_3_out, ~F[2], ~F[1], ~F[0]);  // AND_Gate
  D_Flip_Flop C2 (.D(or_1_out), .clk(clock_1_out), .Q(F[2]));  // open: Qn, preset, reset
  or or_1 (or_1_out, and_1_out, and_2_out, and_3_out);
endmodule

module F11 (
);

  wire alarmafrigorifico_1_alarma, clock_1_out, por_1_out;
  wire [3:0] slider_1_out;

  Clock clock_1 (.out(clock_1_out));
  Slider #(.width(4)) slider_1 (.out(slider_1_out));
  AlarmaFrigorifico alarmafrigorifico_1 (
    .Temp(slider_1_out), .Clk(clock_1_out), .R(por_1_out), .Alarma(alarmafrigorifico_1_alarma));
  POR por_1 (.out(por_1_out));
  LED led_1 (.in(alarmafrigorifico_1_alarma));
endmodule

module AlarmaFrigorifico (
  input  [3:0] Temp,
  input  Clk,
  input  R,
  output Alarma
);

  wire NS0, S0;

  ROM #(.addrWidth(5), .dataWidth(2)) rom_1 (.addr({S0, Temp}), .data({Alarma, NS0}));
  D_Flip_Flop d_ff_1 (.D(NS0), .clk(Clk), .Q(S0), .reset(R));  // open: Qn, preset

  // Notes on the sheet:
  //   contents of rom_1 (hex, n*v repeats v):
  //   13*0 3 3 3 8*0 8*3
endmodule

module F12 (
);

  wire clock_1_out, multiplexer_1_out, multiplexer_2_out, multiplexer_3_out;
  wire [2:0] Sel;

  Clock clock_1 (.out(clock_1_out));
  D_Flip_Flop d_ff_1 (.D(multiplexer_1_out), .clk(clock_1_out), .Q(Sel[2]));  // open: Qn, preset, reset
  Multiplexer #(.select(3)) multiplexer_1 (
    .in0(1'b0), .in1(1'b0), .in2(1'b0), .in3(1'b1), .in4(1'b1), .in5(1'b1), .in6(1'b1), .in7(1'b0),
    .out(multiplexer_1_out), .sel(Sel));
  LED led_1 (.in(Sel[2]));
  Multiplexer #(.select(3)) multiplexer_2 (
    .in0(1'b0), .in1(1'b1), .in2(1'b1), .in3(1'b0), .in4(1'b0), .in5(1'b1), .in6(1'b1), .in7(1'b0),
    .out(multiplexer_2_out), .sel(Sel));
  D_Flip_Flop d_ff_2 (.D(multiplexer_2_out), .clk(clock_1_out), .Q(Sel[1]));  // open: Qn, preset, reset
  LED led_2 (.in(Sel[1]));
  Multiplexer #(.select(3)) multiplexer_3 (
    .in0(1'b1), .in1(1'b0), .in2(1'b1), .in3(1'b0), .in4(1'b1), .in5(1'b0), .in6(1'b1), .in7(1'b0),
    .out(multiplexer_3_out), .sel(Sel));
  D_Flip_Flop d_ff_3 (.D(multiplexer_3_out), .clk(clock_1_out), .Q(Sel[0]));  // open: Qn, preset, reset
  LED led_3 (.in(Sel[0]));
endmodule

module F13 (
);

  wire clock_1_out, multiplexer_1_out, multiplexer_2_out, multiplexer_3_out;
  wire [2:0] Sel;

  Clock clock_1 (.out(clock_1_out));
  D_Flip_Flop d_ff_1 (.D(multiplexer_1_out), .clk(clock_1_out), .Q(Sel[2]));  // open: Qn, preset, reset
  Multiplexer #(.select(3)) multiplexer_1 (
    .in0(1'b1), .in1(1'b0), .in2(1'b0), .in3(1'b0), .in4(1'b0), .in5(1'b1), .in6(1'b1), .in7(1'b1),
    .out(multiplexer_1_out), .sel(Sel));
  LED led_1 (.in(Sel[2]));
  Multiplexer #(.select(3)) multiplexer_2 (
    .in0(1'b1), .in1(1'b0), .in2(1'b0), .in3(1'b1), .in4(1'b1), .in5(1'b0), .in6(1'b0), .in7(1'b1),
    .out(multiplexer_2_out), .sel(Sel));
  D_Flip_Flop d_ff_2 (.D(multiplexer_2_out), .clk(clock_1_out), .Q(Sel[1]));  // open: Qn, preset, reset
  LED led_2 (.in(Sel[1]));
  Multiplexer #(.select(3)) multiplexer_3 (
    .in0(1'b1), .in1(1'b0), .in2(1'b1), .in3(1'b0), .in4(1'b1), .in5(1'b0), .in6(1'b1), .in7(1'b0),
    .out(multiplexer_3_out), .sel(Sel));
  D_Flip_Flop d_ff_3 (.D(multiplexer_3_out), .clk(clock_1_out), .Q(Sel[0]));  // open: Qn, preset, reset
  LED led_3 (.in(Sel[0]));
endmodule

module F14 (
);

  wire clock_1_out, multiplexer_1_out, multiplexer_2_out, multiplexer_3_out;
  wire [2:0] Sel;

  Clock clock_1 (.out(clock_1_out));
  D_Flip_Flop d_ff_1 (.D(multiplexer_1_out), .clk(clock_1_out), .Q(Sel[2]));  // open: Qn, preset, reset
  Multiplexer #(.select(3)) multiplexer_1 (
    .in0(1'b0), .in1(1'b0), .in2(1'b0), .in3(1'b1), .in4(1'b0), .out(multiplexer_1_out), .sel(Sel));  // open: in5, in6, in7
  LED led_1 (.in(Sel[2]));
  Multiplexer #(.select(3)) multiplexer_2 (
    .in0(1'b0), .in1(1'b1), .in2(1'b1), .in3(1'b0), .in4(1'b0), .out(multiplexer_2_out), .sel(Sel));  // open: in5, in6, in7
  D_Flip_Flop d_ff_2 (.D(multiplexer_2_out), .clk(clock_1_out), .Q(Sel[1]));  // open: Qn, preset, reset
  LED led_2 (.in(Sel[1]));
  Multiplexer #(.select(3)) multiplexer_3 (
    .in0(1'b1), .in1(1'b0), .in2(1'b1), .in3(1'b0), .in4(1'b0), .out(multiplexer_3_out), .sel(Sel));  // open: in5, in6, in7
  D_Flip_Flop d_ff_3 (.D(multiplexer_3_out), .clk(clock_1_out), .Q(Sel[0]));  // open: Qn, preset, reset
  LED led_3 (.in(Sel[0]));
endmodule

module F15 (
  input  A,
  output F
);

  wire clock_1_out, dipswitch_1_p1, dipswitch_1_p2, dipswitch_1_p3, dipswitch_1_p4, dipswitch_1_p5,
       dipswitch_1_p6, dipswitch_1_p7, dipswitch_1_p8, dipswitch_2_p1, dipswitch_2_p2, dipswitch_2_p3,
       dipswitch_2_p4, dipswitch_2_p5, dipswitch_2_p6, dipswitch_2_p7, dipswitch_2_p8, dipswitch_3_p1,
       dipswitch_3_p2, dipswitch_3_p3, dipswitch_3_p4, multiplexer_1_out, multiplexer_2_out, S0, S1;

  // DipSwitch dipswitch_1: pin names not known; wires that end beside it: dipswitch_1_p1, dipswitch_1_p2, dipswitch_1_p3, dipswitch_1_p4, dipswitch_1_p5, dipswitch_1_p6, dipswitch_1_p7, dipswitch_1_p8
  D_Flip_Flop d_ff_1 (.D(multiplexer_1_out), .clk(clock_1_out), .Q(S1));  // open: Qn, preset, reset
  Multiplexer #(.select(3)) multiplexer_1 (
    .in0(dipswitch_1_p1), .in1(dipswitch_1_p2), .in2(dipswitch_1_p3), .in3(dipswitch_1_p4),
    .in4(dipswitch_1_p5), .in5(dipswitch_1_p6), .in6(dipswitch_1_p7), .in7(dipswitch_1_p8),
    .out(multiplexer_1_out), .sel({S1, S0, A}));
  Clock clock_1 (.out(clock_1_out));
  // DipSwitch dipswitch_2: pin names not known; wires that end beside it: dipswitch_2_p1, dipswitch_2_p2, dipswitch_2_p3, dipswitch_2_p4, dipswitch_2_p5, dipswitch_2_p6, dipswitch_2_p7, dipswitch_2_p8
  // DipSwitch #(.number(4)) dipswitch_3: pin names not known; wires that end beside it: dipswitch_3_p1, dipswitch_3_p2, dipswitch_3_p3, dipswitch_3_p4
  Multiplexer #(.select(3)) multiplexer_2 (
    .in0(dipswitch_2_p1), .in1(dipswitch_2_p2), .in2(dipswitch_2_p3), .in3(dipswitch_2_p4),
    .in4(dipswitch_2_p5), .in5(dipswitch_2_p6), .in6(dipswitch_2_p7), .in7(dipswitch_2_p8),
    .out(multiplexer_2_out), .sel({S1, S0, A}));
  Multiplexer #(.select(2)) multiplexer_3 (
    .in0(dipswitch_3_p1), .in1(dipswitch_3_p2), .in2(dipswitch_3_p3), .in3(dipswitch_3_p4), .out(F),
    .sel({S1, S0}));
  D_Flip_Flop d_ff_2 (.D(multiplexer_2_out), .clk(clock_1_out), .Q(S0));  // open: Qn, preset, reset
endmodule
