// Logisim project TecladoCajaFuerteProgramable.circ as structural Verilog: 3 circuits, main circuit main
module main (
);

  wire D0, D1, D2, D3, D4, D5, D6, D7, D8, D9, DA, encoderclk_1_clk, fsm_1_puerta, por_1_out;
  wire [3:0] encoderclk_1_e, fsm_1_estado;

  Hex_Digit_Display hex_digit_display_1 (.value(encoderclk_1_e));  // open: dp
  EncoderClk encoderclk_1 (
    .D0(D0), .D1(D1), .D2(D2), .D3(D3), .D4(D4), .D5(D5), .D6(D6), .D7(D7), .D8(D8), .D9(D9), .DA(DA),
    .E(encoderclk_1_e), .Clk(encoderclk_1_clk));
  POR por_1 (.out(por_1_out));
  Button button_1 (.out(D1));
  Button button_2 (.out(D4));
  Button button_3 (.out(D7));
  Button button_4 (.out(DA));
  Button button_5 (.out(D2));
  Button button_6 (.out(D5));
  Button button_7 (.out(D8));
  Button button_8 (.out(D0));
  Button button_9 (.out(D3));
  Button button_10 (.out(D6));
  Button button_11 (.out(D9));
  Hex_Digit_Display hex_digit_display_2 (.value(fsm_1_estado));  // open: dp
  FSM fsm_1 (
    .Clk(encoderclk_1_clk), .Reset(por_1_out), .E(encoderclk_1_e), .Estado(fsm_1_estado),
    .Puerta(fsm_1_puerta));
  LED Abrir (.in(fsm_1_puerta));
endmodule

module EncoderClk (
  input  D0,
  input  D1,
  input  D2,
  input  D3,
  input  D4,
  input  D5,
  input  D6,
  input  D7,
  input  D8,
  input  D9,
  input  DA,
  output [3:0] E,
  output Clk
);

  or or_1 (E[0], D1, D3, D5, D7, D9);
  or or_2 (Clk, D0, D1, D2, D3, D4, D5, D6, D7, D8, D9, DA);
  or or_3 (E[1], D2, D3, D6, D7, DA);
  or or_4 (E[2], D4, D5, D6, D7);
  or or_5 (E[3], D8, D9, DA);
endmodule

module FSM (
  input  Clk,
  input  Reset,
  input  [3:0] E,
  output [3:0] Estado,
  output Puerta
);

  wire NS0, NS1, NS2;

  ROM #(.addrWidth(7), .dataWidth(4)) rom_1 (.addr({Estado[2:0], E}), .data({Puerta, NS2, NS1, NS0}));
  D_Flip_Flop #(.trigger("falling")) S0 (.D(NS0), .clk(Clk), .Q(Estado[0]), .reset(Reset));  // open: Qn, preset
  D_Flip_Flop #(.trigger("falling")) S1 (.D(NS1), .clk(Clk), .Q(Estado[1]), .reset(Reset));  // open: Qn, preset
  D_Flip_Flop #(.trigger("falling")) S2 (.D(NS2), .clk(Clk), .Q(Estado[2]), .reset(Reset));  // open: Qn, preset

  assign Estado[3] = 1'b0;

  // Other names for the same wires on the sheet: S0 = Estado[0]; S1 = Estado[1]; S2 = Estado[2]

  // Notes on the sheet:
  //   contents of rom_1 (hex, n*v repeats v):
  //   10*0 1 5*0 2 9*6 1 5*0 6 6 3 7*6 1 5*0 9*6 4 1 5*0 4*6 5 5*6 1 5*0 10*e 9 5*0 10*6 1
endmodule
