// Logisim project Temperatura.circ as structural Verilog: 2 circuits, main circuit main
module main (
);

  wire clock_1_out, fsm_1_alarma, por_1_out;
  wire [3:0] Termometro_out;

  Clock clock_1 (.out(clock_1_out));
  Slider #(.width(4)) Termometro (.out(Termometro_out));
  POR por_1 (.out(por_1_out));
  FSM fsm_1 (.Clk(clock_1_out), .Temp(Termometro_out), .Reset(por_1_out), .Alarma(fsm_1_alarma));
  LED Alarma (.in(fsm_1_alarma));
endmodule

module FSM (
  input  Clk,
  input  [3:0] Temp,
  input  Reset,
  output Alarma
);

  wire S0;
  wire [0:0] rom_1_data;

  ROM #(.addrWidth(5), .dataWidth(2)) rom_1 (.addr({S0, Temp}), .data({Alarma, rom_1_data[0]}));
  D_Flip_Flop d_ff_1 (.D(rom_1_data[0]), .clk(Clk), .Q(S0), .reset(Reset));  // open: Qn, preset

  // Notes on the sheet:
  //   contents of rom_1 (hex, n*v repeats v):
  //   13*0 3 3 3 8*0 8*3
endmodule
